// Digital circuit LEG.dig as structural Verilog
module LEG (
  input  C_0,
  input  C_1,
  input  C_2,
  input  [7:0] A_0,
  input  [7:0] B_0,
  input  clk,
  input  [7:0] Num_1,
  input  In_3,
  input  In_2,
  input  In_1,
  input  [7:0] in_13,
  output [7:0] O_0,
  output Out_0
);

  wire and_1_out, and_2_out, and_3_out, and_4_out, and_5_out, and_6_out, and_7_out, and_8_out, and_9_out,
       and_10_out, and_11_out, and_12_out, and_13_out, and_14_out, and_15_out, and_16_out, and_17_out,
       and_18_out, and_19_out, and_20_out, and_21_out, and_22_out, and_23_out, and_24_out, and_25_out,
       and_26_out, and_27_out, and_28_out, and_29_out, and_30_out, and_31_out, and_32_out, and_33_out,
       and_34_out, and_35_out, and_36_out, and_37_out, and_38_out, and_39_out, and_40_out, and_41_out,
       and_42_out, and_43_out, and_44_out, and_45_out, and_46_out, and_47_out, and_48_out, and_49_out,
       and_50_out, and_51_out, and_52_out, and_53_out, and_54_out, and_55_out, and_56_out, and_57_out,
       and_58_out, and_59_out, and_60_out, and_61_out, and_62_out, and_63_out, and_64_out, and_65_out,
       and_66_out, and_67_out, and_68_out, and_69_out, and_70_out, and_71_out, and_72_out, and_73_out,
       and_74_out, and_207_out, and_208_out, and_209_out, and_210_out, and_211_out, and_212_out, and_213_out,
       and_227_out, and_228_out, and_229_out, and_230_out, and_231_out, and_232_out, and_233_out,
       and_234_out, and_235_out, and_236_out, and_237_out, and_238_out, and_239_out, and_240_out,
       and_241_out, and_242_out, and_243_out, and_244_out, and_245_out, and_246_out, and_247_out,
       and_248_out, and_249_out, and_251_out, and_252_out, and_253_out, and_254_out, and_261_out,
       and_262_out, and_263_out, and_264_out, and_265_out, and_266_out, and_267_out, and_268_out,
       and_270_out, and_271_out, and_272_out, and_273_out, and_275_out, and_276_out, and_277_out,
       and_278_out, and_321_out, and_322_out, and_323_out, and_324_out, and_325_out, and_326_out,
       and_327_out, and_328_out, and_333_out, and_334_out, and_335_out, and_336_out, and_337_out,
       and_338_out, and_339_out, and_343_out, and_344_out, and_345_out, and_346_out, and_347_out,
       and_348_out, and_349_out, and_350_out, and_351_out, and_352_out, and_353_out, and_354_out,
       and_355_out, and_356_out, and_357_out, and_358_out, and_359_out, and_360_out, and_361_out,
       and_362_out, and_363_out, and_364_out, and_365_out, and_366_out, and_367_out, and_368_out,
       and_369_out, and_370_out, and_371_out, and_372_out, and_373_out, and_374_out, and_375_out,
       and_376_out, and_377_out, and_378_out, and_379_out, and_380_out, and_381_out, and_382_out,
       and_383_out, and_384_out, and_385_out, and_386_out, and_387_out, and_388_out, and_389_out,
       and_390_out, and_391_out, and_392_out, and_393_out, and_394_out, and_395_out, and_396_out,
       and_397_out, and_398_out, and_399_out, and_400_out, and_401_out, and_402_out, and_403_out,
       and_404_out, and_405_out, and_406_out, and_407_out, and_408_out, and_409_out, and_410_out,
       and_411_out, and_412_out, and_413_out, and_415_out, and_416_out, and_417_out, and_418_out,
       and_419_out, and_420_out, and_421_out, and_422_out, and_423_out, and_424_out, and_425_out,
       and_426_out, and_427_out, and_428_out, and_429_out, and_430_out, and_431_out, and_432_out,
       and_433_out, and_434_out, and_435_out, and_436_out, and_437_out, and_438_out, and_439_out,
       and_440_out, and_441_out, and_442_out, and_443_out, and_444_out, and_445_out, and_446_out,
       and_447_out, and_448_out, and_449_out, dipswitch_1_out, dipswitch_2_out, dipswitch_3_out,
       dipswitch_4_out, dipswitch_5_out, dipswitch_6_out, dipswitch_7_out, nand_1_out, nand_2_out,
       nand_3_out, nand_4_out, nand_5_out, nand_6_out, nand_7_out, nand_8_out, nand_9_out, nand_10_out,
       nand_11_out, nand_12_out, nand_13_out, nand_14_out, nand_15_out, nand_16_out, nand_17_out,
       nand_18_out, nand_19_out, nand_20_out, nand_21_out, nand_22_out, nand_23_out, nand_24_out,
       nand_25_out, nand_26_out, nand_27_out, nand_28_out, nand_29_out, nand_30_out, nand_31_out,
       nand_32_out, nand_33_out, nand_34_out, nand_35_out, nand_36_out, nand_37_out, nand_38_out,
       nand_39_out, nand_40_out, nand_41_out, nand_42_out, nand_43_out, nand_44_out, nand_45_out,
       nand_46_out, nand_47_out, nand_48_out, nand_49_out, nand_50_out, nand_51_out, nand_52_out,
       nand_53_out, nand_54_out, nand_55_out, nand_56_out, nand_57_out, nand_58_out, nand_59_out,
       nand_60_out, nand_61_out, nand_62_out, nand_63_out, nand_64_out, nand_65_out, nand_66_out,
       nand_67_out, nand_68_out, nand_69_out, nand_70_out, nand_71_out, nand_72_out, nand_73_out,
       nand_74_out, nand_75_out, nand_76_out, nand_77_out, nand_78_out, nand_79_out, nand_80_out,
       nand_81_out, nand_82_out, nand_83_out, nand_84_out, nand_85_out, nand_86_out, nand_87_out,
       nand_88_out, nand_89_out, nand_90_out, nand_91_out, nand_92_out, nand_93_out, nand_94_out,
       nand_95_out, nand_96_out, nand_97_out, nand_98_out, nand_99_out, nand_100_out, nand_101_out,
       nand_102_out, nand_103_out, nand_104_out, nand_105_out, nand_106_out, nand_107_out, nand_108_out,
       nand_109_out, nand_110_out, nand_111_out, nand_112_out, nand_113_out, nand_114_out, nand_115_out,
       nand_116_out, nand_117_out, nand_118_out, nand_119_out, nand_120_out, nand_121_out, nand_122_out,
       nand_123_out, nand_124_out, nand_125_out, nand_126_out, nand_127_out, nand_128_out, nand_129_out,
       nand_130_out, nand_131_out, nand_132_out, nand_133_out, nand_134_out, nand_135_out, nand_136_out,
       nand_137_out, nand_138_out, nand_139_out, nand_140_out, nand_141_out, nand_142_out, nand_143_out,
       nand_144_out, nand_145_out, nand_146_out, nand_147_out, nand_148_out, nand_149_out, nand_150_out,
       nand_151_out, nand_152_out, nand_153_out, nand_154_out, nand_155_out, nand_156_out, nand_157_out,
       nand_158_out, nand_159_out, nand_160_out, nand_161_out, nand_162_out, nand_163_out, nand_164_out,
       nand_165_out, nand_166_out, nand_167_out, nand_168_out, nand_169_out, nand_170_out, nand_171_out,
       nand_172_out, nand_173_out, nand_174_out, nand_175_out, nand_176_out, nand_177_out, nand_178_out,
       nand_179_out, nand_180_out, nand_181_out, nand_182_out, nand_183_out, nand_184_out, nand_185_out,
       nand_186_out, nand_187_out, nand_188_out, nand_189_out, nand_190_out, nand_191_out, nand_192_out,
       nand_193_out, nand_194_out, nand_195_out, nand_196_out, nand_197_out, nand_198_out, nand_199_out,
       nand_200_out, nand_201_out, nand_202_out, nand_203_out, nand_204_out, nand_205_out, nand_206_out,
       nand_207_out, nand_208_out, nand_209_out, nand_210_out, nand_211_out, nand_212_out, nand_213_out,
       nand_214_out, nand_215_out, nand_216_out, nand_217_out, nand_218_out, nand_219_out, nand_220_out,
       nand_221_out, nand_222_out, nand_223_out, nand_224_out, nand_225_out, nand_226_out, nand_227_out,
       nand_228_out, nand_229_out, nand_230_out, nand_231_out, nand_232_out, nand_233_out, nand_234_out,
       nand_235_out, nand_236_out, nand_237_out, nand_238_out, nand_239_out, nand_240_out, nand_241_out,
       nand_242_out, nand_243_out, nand_244_out, nand_245_out, nand_246_out, nand_247_out, nand_248_out,
       nand_249_out, nand_250_out, nand_251_out, nand_252_out, nand_253_out, nand_254_out, nand_255_out,
       nand_256_out, nand_257_out, nand_258_out, nand_259_out, nand_260_out, nand_261_out, nand_262_out,
       nand_263_out, nand_264_out, nand_265_out, nand_266_out, nand_267_out, nand_268_out, nand_269_out,
       nand_270_out, nand_271_out, nand_272_out, nand_273_out, nand_274_out, nand_275_out, nand_276_out,
       nand_277_out, nand_278_out, nand_279_out, nand_280_out, nand_281_out, nand_282_out, nand_283_out,
       nand_284_out, nand_285_out, nand_286_out, nand_287_out, nand_288_out, nand_289_out, nand_290_out,
       nand_291_out, nand_292_out, nand_293_out, nand_294_out, nand_295_out, nand_296_out, nand_297_out,
       nand_298_out, nand_299_out, nand_300_out, nand_301_out, nand_302_out, nand_303_out, nand_304_out,
       nand_306_out, nand_308_out, nand_310_out, nand_312_out, nand_313_out, nand_314_out, nand_315_out,
       nand_316_out, nand_317_out, nand_318_out, nand_319_out, nand_320_out, nand_321_out, nand_322_out,
       nand_323_out, nand_324_out, nand_325_out, nand_326_out, nand_327_out, nand_328_out, nand_330_out,
       nand_332_out, nand_334_out, nand_336_out, nand_345_out, nand_346_out, nand_347_out, nand_348_out,
       nand_349_out, nand_350_out, nand_351_out, nand_352_out, nand_353_out, nand_354_out, nand_355_out,
       nand_356_out, nand_357_out, nand_358_out, nand_359_out, nand_360_out, nand_361_out, nand_362_out,
       nand_363_out, nand_364_out, nand_365_out, nand_366_out, nand_367_out, nand_368_out, nand_369_out,
       nand_370_out, nand_371_out, nand_372_out, nand_373_out, nand_374_out, nand_375_out, nand_376_out,
       nand_377_out, nand_378_out, nand_379_out, nand_380_out, nand_381_out, nand_382_out, nand_383_out,
       nand_384_out, nand_385_out, nand_386_out, nand_387_out, nand_388_out, nand_389_out, nand_390_out,
       nand_391_out, nand_392_out, nand_393_out, nand_394_out, nand_395_out, nand_396_out, nand_397_out,
       nand_398_out, nand_399_out, nand_400_out, nand_401_out, nand_402_out, nand_403_out, nand_404_out,
       nand_405_out, nand_406_out, nand_407_out, nand_408_out, nand_409_out, nand_410_out, nand_411_out,
       nand_412_out, nand_413_out, nand_414_out, nand_415_out, nand_416_out, nand_417_out, nand_418_out,
       nand_419_out, nand_420_out, nand_421_out, nand_422_out, nand_423_out, nand_424_out, nand_425_out,
       nand_426_out, nand_427_out, nand_428_out, nand_429_out, nand_430_out, nand_431_out, nand_432_out,
       nand_433_out, nand_434_out, nand_435_out, nand_436_out, nand_437_out, nand_438_out, nand_439_out,
       nand_440_out, nand_441_out, nand_442_out, nand_443_out, nand_444_out, nand_445_out, nand_446_out,
       nand_447_out, nand_448_out, nor_9_out, nor_10_out, nor_11_out, nor_12_out, nor_13_out, nor_14_out,
       nor_15_out, nor_16_out, nor_17_out, nor_18_out, nor_19_out, nor_20_out, nor_21_out, nor_22_out,
       nor_23_out, nor_24_out, nor_25_out, nor_26_out, nor_27_out, nor_28_out, nor_29_out, nor_30_out,
       nor_31_out, nor_32_out, nor_33_out, nor_34_out, not_1_out, not_2_out, not_3_out, not_4_out, not_5_out,
       not_6_out, not_7_out, not_8_out, not_9_out, not_10_out, not_11_out, not_12_out, not_13_out,
       not_14_out, not_15_out, not_16_out, not_17_out, not_18_out, not_19_out, not_20_out, not_21_out,
       not_22_out, not_23_out, not_24_out, not_25_out, not_26_out, not_27_out, not_28_out, not_29_out,
       not_30_out, not_31_out, not_32_out, not_33_out, not_34_out, not_35_out, not_36_out, not_37_out,
       not_38_out, not_39_out, not_40_out, not_41_out, not_42_out, not_43_out, not_44_out, not_45_out,
       not_46_out, not_47_out, not_48_out, not_49_out, not_50_out, not_51_out, not_52_out, not_53_out,
       not_54_out, not_55_out, not_56_out, not_57_out, not_58_out, not_59_out, not_60_out,
       notconnected_2_out, notconnected_3_out, notconnected_4_out, notconnected_5_out, notconnected_9_out,
       notconnected_14_out, notconnected_18_out, notconnected_19_out, notconnected_20_out,
       notconnected_21_out, or_9_out, or_10_out, or_11_out, or_12_out, or_13_out, or_14_out, or_15_out,
       or_16_out, or_17_out, or_18_out, or_19_out, or_20_out, or_21_out, or_22_out, or_23_out, or_25_out,
       or_26_out, or_34_out, or_35_out, or_36_out, or_37_out, or_38_out, or_39_out, or_40_out, or_41_out,
       or_43_out, or_84_out, or_85_out, or_86_out, or_87_out, or_88_out, or_89_out, or_90_out, or_91_out,
       or_92_out, or_93_out, or_94_out, or_95_out, or_96_out, or_97_out, or_98_out, or_99_out, undriven_6,
       xor_9_out, xor_10_out, xor_11_out, xor_12_out, xor_13_out, xor_14_out, xor_15_out, xor_16_out,
       xor_23_out, xor_24_out, xor_25_out, xor_26_out, xor_27_out, xor_28_out, xor_29_out, xor_30_out,
       xor_41_out, xor_42_out, xor_43_out, xor_44_out, xor_45_out, xor_46_out, xor_47_out, xor_48_out,
       xor_49_out, xor_50_out, xor_51_out, xor_52_out, xor_53_out, xor_54_out, xor_55_out, xor_56_out,
       xor_57_out, xor_58_out, xor_59_out, xor_60_out, xor_61_out, xor_62_out, xor_63_out, xor_64_out,
       xor_65_out, xor_66_out, xor_67_out, xor_68_out, xor_69_out, xor_70_out, xor_71_out, xor_72_out;
  wire [2:0] undriven_3;
  wire [7:0] and_75_out, and_76_out, and_218_out, and_226_out, and_274_out, and_314_out, and_315_out,
       and_316_out, and_317_out, and_318_out, and_342_out, nand_335_out, nand_344_out, nor_8_out,
       notconnected_1_out, notconnected_6_out, notconnected_7_out, notconnected_8_out, notconnected_10_out,
       notconnected_11_out, notconnected_12_out, notconnected_13_out, notconnected_15_out,
       notconnected_16_out, notconnected_17_out, or_8_out, or_42_out, or_80_out, or_81_out, or_82_out,
       or_83_out, rom_1_d, undriven, undriven_2, undriven_4, xor_8_out, xor_36_out, xor_40_out;
  wire [7:4] undriven_5;

  not not_1 (not_1_out, undriven_3[0]);
  not not_2 (not_2_out, not_1_out);
  and and_1 (and_1_out, and_4_out, not_2_out);
  and and_2 (and_2_out, not_8_out, and_1_out);
  and and_3 (and_3_out, not_4_out, undriven_3[1]);
  and and_4 (and_4_out, undriven_3[1], undriven_3[2]);
  and and_5 (and_5_out, and_3_out, not_2_out);
  and and_6 (and_6_out, not_8_out, and_5_out);
  and and_7 (and_7_out, undriven_3[2], not_3_out);
  and and_8 (and_8_out, and_7_out, not_2_out);
  and and_9 (and_9_out, not_8_out, and_8_out);
  and and_10 (and_10_out, not_4_out, not_3_out);
  and and_11 (and_11_out, and_10_out, not_2_out);
  and and_12 (and_12_out, not_8_out, and_11_out);
  not not_3 (not_3_out, undriven_3[1]);
  not not_4 (not_4_out, undriven_3[2]);
  not not_5 (not_5_out, undriven_3[0]);
  and and_13 (and_13_out, undriven_3[1], undriven_3[2]);
  and and_14 (and_14_out, and_19_out, not_5_out);
  and and_15 (and_15_out, and_13_out, not_5_out);
  and and_16 (and_16_out, not_8_out, and_14_out);
  and and_17 (and_17_out, not_8_out, and_15_out);
  and and_18 (and_18_out, undriven_3[2], not_6_out);
  and and_19 (and_19_out, not_7_out, undriven_3[1]);
  and and_20 (and_20_out, and_18_out, not_5_out);
  and and_21 (and_21_out, not_8_out, and_20_out);
  and and_22 (and_22_out, not_7_out, not_6_out);
  and and_23 (and_23_out, and_22_out, not_5_out);
  and and_24 (and_24_out, not_8_out, and_23_out);
  not not_6 (not_6_out, undriven_3[1]);
  not not_7 (not_7_out, undriven_3[2]);
  not not_8 (not_8_out, undriven_6);
  not not_9 (not_9_out, undriven_2[0]);
  not not_10 (not_10_out, not_9_out);
  and and_25 (and_25_out, undriven_2[1], undriven_2[2]);
  and and_26 (and_26_out, and_25_out, not_10_out);
  and and_27 (and_27_out, not_18_out, and_26_out);
  and and_28 (and_28_out, not_12_out, undriven_2[1]);
  and and_29 (and_29_out, and_28_out, not_10_out);
  and and_30 (and_30_out, not_18_out, and_29_out);
  and and_31 (and_31_out, undriven_2[2], not_11_out);
  and and_32 (and_32_out, and_36_out, not_10_out);
  and and_33 (and_33_out, and_31_out, not_10_out);
  and and_34 (and_34_out, not_18_out, and_32_out);
  and and_35 (and_35_out, not_18_out, and_33_out);
  and and_36 (and_36_out, not_12_out, not_11_out);
  not not_11 (not_11_out, undriven_2[1]);
  not not_12 (not_12_out, undriven_2[2]);
  and and_37 (and_37_out, not_13_out, not_14_out);
  not not_13 (not_13_out, undriven_5[5]);
  not not_14 (not_14_out, undriven_5[4]);
  and and_38 (and_38_out, not_14_out, undriven_5[5]);
  not not_15 (not_15_out, undriven_2[0]);
  and and_39 (and_39_out, and_42_out, not_15_out);
  and and_40 (and_40_out, not_18_out, and_39_out);
  and and_41 (and_41_out, not_17_out, undriven_2[1]);
  and and_42 (and_42_out, undriven_2[1], undriven_2[2]);
  and and_43 (and_43_out, and_41_out, not_15_out);
  and and_44 (and_44_out, not_18_out, and_43_out);
  and and_45 (and_45_out, undriven_2[2], not_16_out);
  and and_46 (and_46_out, and_45_out, not_15_out);
  and and_47 (and_47_out, not_18_out, and_46_out);
  and and_48 (and_48_out, not_17_out, not_16_out);
  and and_49 (and_49_out, and_48_out, not_15_out);
  and and_50 (and_50_out, not_18_out, and_49_out);
  not not_16 (not_16_out, undriven_2[1]);
  not not_17 (not_17_out, undriven_2[2]);
  not not_18 (not_18_out, undriven_5[6]);
  not not_19 (not_19_out, undriven_4[0]);
  not not_20 (not_20_out, not_19_out);
  and and_51 (and_51_out, and_54_out, not_20_out);
  and and_52 (and_52_out, not_26_out, and_51_out);
  and and_53 (and_53_out, not_22_out, undriven_4[1]);
  and and_54 (and_54_out, undriven_4[1], undriven_4[2]);
  and and_55 (and_55_out, and_53_out, not_20_out);
  and and_56 (and_56_out, not_26_out, and_55_out);
  and and_57 (and_57_out, undriven_4[2], not_21_out);
  and and_58 (and_58_out, and_57_out, not_20_out);
  and and_59 (and_59_out, not_26_out, and_58_out);
  and and_60 (and_60_out, not_22_out, not_21_out);
  and and_61 (and_61_out, and_60_out, not_20_out);
  and and_62 (and_62_out, not_26_out, and_61_out);
  not not_21 (not_21_out, undriven_4[1]);
  not not_22 (not_22_out, undriven_4[2]);
  not not_23 (not_23_out, undriven_4[0]);
  and and_63 (and_63_out, undriven_4[1], undriven_4[2]);
  and and_64 (and_64_out, and_69_out, not_23_out);
  and and_65 (and_65_out, and_63_out, not_23_out);
  and and_66 (and_66_out, not_26_out, and_64_out);
  and and_67 (and_67_out, not_26_out, and_65_out);
  and and_68 (and_68_out, undriven_4[2], not_24_out);
  and and_69 (and_69_out, not_25_out, undriven_4[1]);
  and and_70 (and_70_out, and_68_out, not_23_out);
  and and_71 (and_71_out, not_26_out, and_70_out);
  and and_72 (and_72_out, not_25_out, not_24_out);
  and and_73 (and_73_out, and_72_out, not_23_out);
  and and_74 (and_74_out, not_26_out, and_73_out);
  not not_24 (not_24_out, undriven_4[1]);
  not not_25 (not_25_out, undriven_4[2]);
  not not_26 (not_26_out, undriven_5[7]);
  ROM #(.AddrBits(8), .Bits(8)) rom_1 (.sel(1'b1), .D(rom_1_d));  // open: A
  and and_75 (and_75_out[0], and_30_out, rom_1_d[0]);
  and and_76 (and_76_out[0], and_56_out, rom_1_d[0]);
  and and_77 (and_75_out[0], undriven_5[6], undriven_2[0]);
  and and_78 (and_75_out[1], undriven_5[6], undriven_2[1]);
  and and_79 (and_76_out[0], undriven_5[7], undriven_4[0]);
  and and_80 (and_76_out[1], undriven_5[7], undriven_4[1]);
  and and_81 (and_75_out[1], and_30_out, rom_1_d[1]);
  and and_82 (and_76_out[1], and_56_out, rom_1_d[1]);
  and and_83 (and_75_out[2], undriven_5[6], undriven_2[2]);
  and and_84 (and_76_out[2], undriven_5[7], undriven_4[2]);
  and and_85 (and_75_out[2], and_30_out, rom_1_d[2]);
  and and_86 (and_76_out[2], and_56_out, rom_1_d[2]);
  and and_87 (and_75_out[3], undriven_5[6], undriven_2[3]);
  and and_88 (and_76_out[3], undriven_5[7], undriven_4[3]);
  and and_89 (and_75_out[3], and_30_out, rom_1_d[3]);
  and and_90 (and_75_out[4], and_30_out, rom_1_d[4]);
  and and_91 (and_76_out[3], and_56_out, rom_1_d[3]);
  and and_92 (and_76_out[4], and_56_out, rom_1_d[4]);
  and and_93 (and_75_out[4], undriven_5[6], undriven_2[4]);
  and and_94 (and_75_out[5], undriven_5[6], undriven_2[5]);
  and and_95 (and_76_out[4], undriven_5[7], undriven_4[4]);
  and and_96 (and_76_out[5], undriven_5[7], undriven_4[5]);
  and and_97 (and_75_out[5], and_30_out, rom_1_d[5]);
  and and_98 (and_76_out[5], and_56_out, rom_1_d[5]);
  and and_99 (and_75_out[6], undriven_5[6], undriven_2[6]);
  and and_100 (and_76_out[6], undriven_5[7], undriven_4[6]);
  and and_101 (and_75_out[6], and_30_out, rom_1_d[6]);
  and and_102 (and_76_out[6], and_56_out, rom_1_d[6]);
  and and_103 (and_75_out[7], undriven_5[6], undriven_2[7]);
  and and_104 (and_76_out[7], undriven_5[7], undriven_4[7]);
  and and_105 (and_75_out[7], and_30_out, rom_1_d[7]);
  and and_106 (and_76_out[7], and_56_out, rom_1_d[7]);
  nand nand_1 (nand_1_out, nand_4_out, nand_2_out);
  nand nand_2 (nand_2_out, nand_1_out, and_24_out);
  nand nand_3 (nand_3_out, nand_2_out, and_24_out, nand_4_out);
  nand nand_4 (nand_4_out, nand_3_out, undriven[6]);
  nand nand_5 (nand_5_out, nand_8_out, nand_6_out);
  nand nand_6 (nand_6_out, nand_5_out, and_24_out);
  nand nand_7 (nand_7_out, nand_6_out, and_24_out, nand_8_out);
  nand nand_8 (nand_8_out, nand_7_out, undriven[4]);
  nand nand_9 (nand_9_out, nand_12_out, nand_10_out);
  nand nand_10 (nand_10_out, nand_9_out, and_24_out);
  nand nand_11 (nand_11_out, nand_10_out, and_24_out, nand_12_out);
  nand nand_12 (nand_12_out, nand_11_out, undriven[2]);
  nand nand_13 (nand_13_out, nand_16_out, nand_14_out);
  nand nand_14 (nand_14_out, nand_13_out, and_24_out);
  nand nand_15 (nand_15_out, nand_14_out, and_24_out, nand_16_out);
  nand nand_16 (nand_16_out, nand_15_out, undriven[0]);
  nand nand_17 (nand_17_out, nand_20_out, nand_18_out);
  nand nand_18 (nand_18_out, nand_17_out, and_21_out);
  nand nand_19 (nand_19_out, nand_18_out, and_21_out, nand_20_out);
  nand nand_20 (nand_20_out, nand_19_out, undriven[6]);
  nand nand_21 (nand_21_out, nand_24_out, nand_22_out);
  nand nand_22 (nand_22_out, nand_21_out, and_21_out);
  nand nand_23 (nand_23_out, nand_22_out, and_21_out, nand_24_out);
  nand nand_24 (nand_24_out, nand_23_out, undriven[4]);
  nand nand_25 (nand_25_out, nand_28_out, nand_26_out);
  nand nand_26 (nand_26_out, nand_25_out, and_21_out);
  nand nand_27 (nand_27_out, nand_26_out, and_21_out, nand_28_out);
  nand nand_28 (nand_28_out, nand_27_out, undriven[2]);
  nand nand_29 (nand_29_out, nand_32_out, nand_30_out);
  nand nand_30 (nand_30_out, nand_29_out, and_21_out);
  nand nand_31 (nand_31_out, nand_30_out, and_21_out, nand_32_out);
  nand nand_32 (nand_32_out, nand_31_out, undriven[0]);
  nand nand_33 (nand_33_out, nand_36_out, nand_34_out);
  nand nand_34 (nand_34_out, nand_33_out, and_16_out);
  nand nand_35 (nand_35_out, nand_34_out, and_16_out, nand_36_out);
  nand nand_36 (nand_36_out, nand_35_out, undriven[6]);
  nand nand_37 (nand_37_out, nand_40_out, nand_38_out);
  nand nand_38 (nand_38_out, nand_37_out, and_16_out);
  nand nand_39 (nand_39_out, nand_38_out, and_16_out, nand_40_out);
  nand nand_40 (nand_40_out, nand_39_out, undriven[4]);
  nand nand_41 (nand_41_out, nand_44_out, nand_42_out);
  nand nand_42 (nand_42_out, nand_41_out, and_16_out);
  nand nand_43 (nand_43_out, nand_42_out, and_16_out, nand_44_out);
  nand nand_44 (nand_44_out, nand_43_out, undriven[2]);
  nand nand_45 (nand_45_out, nand_48_out, nand_46_out);
  nand nand_46 (nand_46_out, nand_45_out, and_16_out);
  nand nand_47 (nand_47_out, nand_46_out, and_16_out, nand_48_out);
  nand nand_48 (nand_48_out, nand_47_out, undriven[0]);
  nand nand_49 (nand_49_out, nand_52_out, nand_50_out);
  nand nand_50 (nand_50_out, nand_49_out, and_17_out);
  nand nand_51 (nand_51_out, nand_50_out, and_17_out, nand_52_out);
  nand nand_52 (nand_52_out, nand_51_out, undriven[6]);
  nand nand_53 (nand_53_out, nand_56_out, nand_54_out);
  nand nand_54 (nand_54_out, nand_53_out, and_17_out);
  nand nand_55 (nand_55_out, nand_54_out, and_17_out, nand_56_out);
  nand nand_56 (nand_56_out, nand_55_out, undriven[4]);
  nand nand_57 (nand_57_out, nand_60_out, nand_58_out);
  nand nand_58 (nand_58_out, nand_57_out, and_17_out);
  nand nand_59 (nand_59_out, nand_58_out, and_17_out, nand_60_out);
  nand nand_60 (nand_60_out, nand_59_out, undriven[2]);
  nand nand_61 (nand_61_out, nand_64_out, nand_62_out);
  nand nand_62 (nand_62_out, nand_61_out, and_17_out);
  nand nand_63 (nand_63_out, nand_62_out, and_17_out, nand_64_out);
  nand nand_64 (nand_64_out, nand_63_out, undriven[0]);
  nand nand_65 (nand_65_out, nand_68_out, nand_66_out);
  nand nand_66 (nand_66_out, nand_65_out, and_12_out);
  nand nand_67 (nand_67_out, nand_66_out, and_12_out, nand_68_out);
  nand nand_68 (nand_68_out, nand_67_out, undriven[6]);
  nand nand_69 (nand_69_out, nand_72_out, nand_70_out);
  nand nand_70 (nand_70_out, nand_69_out, and_12_out);
  nand nand_71 (nand_71_out, nand_70_out, and_12_out, nand_72_out);
  nand nand_72 (nand_72_out, nand_71_out, undriven[4]);
  nand nand_73 (nand_73_out, nand_76_out, nand_74_out);
  nand nand_74 (nand_74_out, nand_73_out, and_12_out);
  nand nand_75 (nand_75_out, nand_74_out, and_12_out, nand_76_out);
  nand nand_76 (nand_76_out, nand_75_out, undriven[2]);
  nand nand_77 (nand_77_out, nand_80_out, nand_78_out);
  nand nand_78 (nand_78_out, nand_77_out, and_12_out);
  nand nand_79 (nand_79_out, nand_78_out, and_12_out, nand_80_out);
  nand nand_80 (nand_80_out, nand_79_out, undriven[0]);
  nand nand_81 (nand_81_out, nand_84_out, nand_82_out);
  nand nand_82 (nand_82_out, nand_81_out, and_9_out);
  nand nand_83 (nand_83_out, nand_82_out, and_9_out, nand_84_out);
  nand nand_84 (nand_84_out, nand_83_out, undriven[6]);
  nand nand_85 (nand_85_out, nand_88_out, nand_86_out);
  nand nand_86 (nand_86_out, nand_85_out, and_9_out);
  nand nand_87 (nand_87_out, nand_86_out, and_9_out, nand_88_out);
  nand nand_88 (nand_88_out, nand_87_out, undriven[4]);
  nand nand_89 (nand_89_out, nand_92_out, nand_90_out);
  nand nand_90 (nand_90_out, nand_89_out, and_9_out);
  nand nand_91 (nand_91_out, nand_90_out, and_9_out, nand_92_out);
  nand nand_92 (nand_92_out, nand_91_out, undriven[2]);
  nand nand_93 (nand_93_out, nand_96_out, nand_94_out);
  nand nand_94 (nand_94_out, nand_93_out, and_9_out);
  nand nand_95 (nand_95_out, nand_94_out, and_9_out, nand_96_out);
  nand nand_96 (nand_96_out, nand_95_out, undriven[0]);
  nand nand_97 (nand_97_out, nand_2_out, nand_98_out);
  nand nand_98 (nand_98_out, nand_97_out, nand_3_out);
  and and_107 (and_76_out[6], nand_97_out, and_74_out);
  and and_108 (and_75_out[6], nand_97_out, and_50_out);
  nand nand_99 (nand_99_out, nand_6_out, nand_100_out);
  nand nand_100 (nand_100_out, nand_99_out, nand_7_out);
  and and_109 (and_76_out[4], nand_99_out, and_74_out);
  and and_110 (and_75_out[4], nand_99_out, and_50_out);
  nand nand_101 (nand_101_out, nand_10_out, nand_102_out);
  nand nand_102 (nand_102_out, nand_101_out, nand_11_out);
  and and_111 (and_76_out[2], nand_101_out, and_74_out);
  and and_112 (and_75_out[2], nand_101_out, and_50_out);
  nand nand_103 (nand_103_out, nand_14_out, nand_104_out);
  nand nand_104 (nand_104_out, nand_103_out, nand_15_out);
  and and_113 (and_76_out[0], nand_103_out, and_74_out);
  and and_114 (and_75_out[0], nand_103_out, and_50_out);
  nand nand_105 (nand_105_out, nand_18_out, nand_106_out);
  nand nand_106 (nand_106_out, nand_105_out, nand_19_out);
  and and_115 (and_76_out[6], nand_105_out, and_71_out);
  and and_116 (and_75_out[6], nand_105_out, and_47_out);
  nand nand_107 (nand_107_out, nand_22_out, nand_108_out);
  nand nand_108 (nand_108_out, nand_107_out, nand_23_out);
  and and_117 (and_76_out[4], nand_107_out, and_71_out);
  and and_118 (and_75_out[4], nand_107_out, and_47_out);
  nand nand_109 (nand_109_out, nand_26_out, nand_110_out);
  nand nand_110 (nand_110_out, nand_109_out, nand_27_out);
  and and_119 (and_76_out[2], nand_109_out, and_71_out);
  and and_120 (and_75_out[2], nand_109_out, and_47_out);
  nand nand_111 (nand_111_out, nand_30_out, nand_112_out);
  nand nand_112 (nand_112_out, nand_111_out, nand_31_out);
  and and_121 (and_76_out[0], nand_111_out, and_71_out);
  and and_122 (and_75_out[0], nand_111_out, and_47_out);
  nand nand_113 (nand_113_out, nand_34_out, nand_114_out);
  nand nand_114 (nand_114_out, nand_113_out, nand_35_out);
  and and_123 (and_76_out[6], nand_113_out, and_66_out);
  and and_124 (and_75_out[6], nand_113_out, and_44_out);
  nand nand_115 (nand_115_out, nand_38_out, nand_116_out);
  nand nand_116 (nand_116_out, nand_115_out, nand_39_out);
  and and_125 (and_76_out[4], nand_115_out, and_66_out);
  and and_126 (and_75_out[4], nand_115_out, and_44_out);
  nand nand_117 (nand_117_out, nand_42_out, nand_118_out);
  nand nand_118 (nand_118_out, nand_117_out, nand_43_out);
  and and_127 (and_76_out[2], nand_117_out, and_66_out);
  and and_128 (and_75_out[2], nand_117_out, and_44_out);
  nand nand_119 (nand_119_out, nand_46_out, nand_120_out);
  nand nand_120 (nand_120_out, nand_119_out, nand_47_out);
  and and_129 (and_76_out[0], nand_119_out, and_66_out);
  and and_130 (and_75_out[0], nand_119_out, and_44_out);
  nand nand_121 (nand_121_out, nand_50_out, nand_122_out);
  nand nand_122 (nand_122_out, nand_121_out, nand_51_out);
  and and_131 (and_76_out[6], nand_121_out, and_67_out);
  and and_132 (and_75_out[6], nand_121_out, and_40_out);
  nand nand_123 (nand_123_out, nand_54_out, nand_124_out);
  nand nand_124 (nand_124_out, nand_123_out, nand_55_out);
  and and_133 (and_76_out[4], nand_123_out, and_67_out);
  and and_134 (and_75_out[4], nand_123_out, and_40_out);
  nand nand_125 (nand_125_out, nand_58_out, nand_126_out);
  nand nand_126 (nand_126_out, nand_125_out, nand_59_out);
  and and_135 (and_76_out[2], nand_125_out, and_67_out);
  and and_136 (and_75_out[2], nand_125_out, and_40_out);
  nand nand_127 (nand_127_out, nand_62_out, nand_128_out);
  nand nand_128 (nand_128_out, nand_127_out, nand_63_out);
  and and_137 (and_76_out[0], nand_127_out, and_67_out);
  and and_138 (and_75_out[0], nand_127_out, and_40_out);
  nand nand_129 (nand_129_out, nand_66_out, nand_130_out);
  nand nand_130 (nand_130_out, nand_129_out, nand_67_out);
  and and_139 (and_76_out[6], nand_129_out, and_62_out);
  and and_140 (and_75_out[6], nand_129_out, and_34_out);
  nand nand_131 (nand_131_out, nand_70_out, nand_132_out);
  nand nand_132 (nand_132_out, nand_131_out, nand_71_out);
  and and_141 (and_76_out[4], nand_131_out, and_62_out);
  and and_142 (and_75_out[4], nand_131_out, and_34_out);
  nand nand_133 (nand_133_out, nand_74_out, nand_134_out);
  nand nand_134 (nand_134_out, nand_133_out, nand_75_out);
  and and_143 (and_76_out[2], nand_133_out, and_62_out);
  and and_144 (and_75_out[2], nand_133_out, and_34_out);
  nand nand_135 (nand_135_out, nand_78_out, nand_136_out);
  nand nand_136 (nand_136_out, nand_135_out, nand_79_out);
  and and_145 (and_76_out[0], nand_135_out, and_62_out);
  and and_146 (and_75_out[0], nand_135_out, and_34_out);
  nand nand_137 (nand_137_out, nand_82_out, nand_138_out);
  nand nand_138 (nand_138_out, nand_137_out, nand_83_out);
  and and_147 (and_76_out[6], nand_137_out, and_59_out);
  and and_148 (and_75_out[6], nand_137_out, and_35_out);
  nand nand_139 (nand_139_out, nand_86_out, nand_140_out);
  nand nand_140 (nand_140_out, nand_139_out, nand_87_out);
  and and_149 (and_76_out[4], nand_139_out, and_59_out);
  and and_150 (and_75_out[4], nand_139_out, and_35_out);
  nand nand_141 (nand_141_out, nand_90_out, nand_142_out);
  nand nand_142 (nand_142_out, nand_141_out, nand_91_out);
  and and_151 (and_76_out[2], nand_141_out, and_59_out);
  and and_152 (and_75_out[2], nand_141_out, and_35_out);
  nand nand_143 (nand_143_out, nand_94_out, nand_144_out);
  nand nand_144 (nand_144_out, nand_143_out, nand_95_out);
  and and_153 (and_76_out[0], nand_143_out, and_59_out);
  and and_154 (and_75_out[0], nand_143_out, and_35_out);
  nand nand_145 (nand_145_out, nand_148_out, nand_146_out);
  nand nand_146 (nand_146_out, nand_145_out, and_24_out);
  nand nand_147 (nand_147_out, nand_146_out, and_24_out, nand_148_out);
  nand nand_148 (nand_148_out, nand_147_out, undriven[7]);
  nand nand_149 (nand_149_out, nand_152_out, nand_150_out);
  nand nand_150 (nand_150_out, nand_149_out, and_24_out);
  nand nand_151 (nand_151_out, nand_150_out, and_24_out, nand_152_out);
  nand nand_152 (nand_152_out, nand_151_out, undriven[5]);
  nand nand_153 (nand_153_out, nand_156_out, nand_154_out);
  nand nand_154 (nand_154_out, nand_153_out, and_24_out);
  nand nand_155 (nand_155_out, nand_154_out, and_24_out, nand_156_out);
  nand nand_156 (nand_156_out, nand_155_out, undriven[3]);
  nand nand_157 (nand_157_out, nand_160_out, nand_158_out);
  nand nand_158 (nand_158_out, nand_157_out, and_24_out);
  nand nand_159 (nand_159_out, nand_158_out, and_24_out, nand_160_out);
  nand nand_160 (nand_160_out, nand_159_out, undriven[1]);
  nand nand_161 (nand_161_out, nand_164_out, nand_162_out);
  nand nand_162 (nand_162_out, nand_161_out, and_21_out);
  nand nand_163 (nand_163_out, nand_162_out, and_21_out, nand_164_out);
  nand nand_164 (nand_164_out, nand_163_out, undriven[7]);
  nand nand_165 (nand_165_out, nand_168_out, nand_166_out);
  nand nand_166 (nand_166_out, nand_165_out, and_21_out);
  nand nand_167 (nand_167_out, nand_166_out, and_21_out, nand_168_out);
  nand nand_168 (nand_168_out, nand_167_out, undriven[5]);
  nand nand_169 (nand_169_out, nand_172_out, nand_170_out);
  nand nand_170 (nand_170_out, nand_169_out, and_21_out);
  nand nand_171 (nand_171_out, nand_170_out, and_21_out, nand_172_out);
  nand nand_172 (nand_172_out, nand_171_out, undriven[3]);
  nand nand_173 (nand_173_out, nand_176_out, nand_174_out);
  nand nand_174 (nand_174_out, nand_173_out, and_21_out);
  nand nand_175 (nand_175_out, nand_174_out, and_21_out, nand_176_out);
  nand nand_176 (nand_176_out, nand_175_out, undriven[1]);
  nand nand_177 (nand_177_out, nand_180_out, nand_178_out);
  nand nand_178 (nand_178_out, nand_177_out, and_16_out);
  nand nand_179 (nand_179_out, nand_178_out, and_16_out, nand_180_out);
  nand nand_180 (nand_180_out, nand_179_out, undriven[7]);
  nand nand_181 (nand_181_out, nand_184_out, nand_182_out);
  nand nand_182 (nand_182_out, nand_181_out, and_16_out);
  nand nand_183 (nand_183_out, nand_182_out, and_16_out, nand_184_out);
  nand nand_184 (nand_184_out, nand_183_out, undriven[5]);
  nand nand_185 (nand_185_out, nand_188_out, nand_186_out);
  nand nand_186 (nand_186_out, nand_185_out, and_16_out);
  nand nand_187 (nand_187_out, nand_186_out, and_16_out, nand_188_out);
  nand nand_188 (nand_188_out, nand_187_out, undriven[3]);
  nand nand_189 (nand_189_out, nand_192_out, nand_190_out);
  nand nand_190 (nand_190_out, nand_189_out, and_16_out);
  nand nand_191 (nand_191_out, nand_190_out, and_16_out, nand_192_out);
  nand nand_192 (nand_192_out, nand_191_out, undriven[1]);
  nand nand_193 (nand_193_out, nand_196_out, nand_194_out);
  nand nand_194 (nand_194_out, nand_193_out, and_17_out);
  nand nand_195 (nand_195_out, nand_194_out, and_17_out, nand_196_out);
  nand nand_196 (nand_196_out, nand_195_out, undriven[7]);
  nand nand_197 (nand_197_out, nand_200_out, nand_198_out);
  nand nand_198 (nand_198_out, nand_197_out, and_17_out);
  nand nand_199 (nand_199_out, nand_198_out, and_17_out, nand_200_out);
  nand nand_200 (nand_200_out, nand_199_out, undriven[5]);
  nand nand_201 (nand_201_out, nand_204_out, nand_202_out);
  nand nand_202 (nand_202_out, nand_201_out, and_17_out);
  nand nand_203 (nand_203_out, nand_202_out, and_17_out, nand_204_out);
  nand nand_204 (nand_204_out, nand_203_out, undriven[3]);
  nand nand_205 (nand_205_out, nand_208_out, nand_206_out);
  nand nand_206 (nand_206_out, nand_205_out, and_17_out);
  nand nand_207 (nand_207_out, nand_206_out, and_17_out, nand_208_out);
  nand nand_208 (nand_208_out, nand_207_out, undriven[1]);
  nand nand_209 (nand_209_out, nand_212_out, nand_210_out);
  nand nand_210 (nand_210_out, nand_209_out, and_12_out);
  nand nand_211 (nand_211_out, nand_210_out, and_12_out, nand_212_out);
  nand nand_212 (nand_212_out, nand_211_out, undriven[7]);
  nand nand_213 (nand_213_out, nand_216_out, nand_214_out);
  nand nand_214 (nand_214_out, nand_213_out, and_12_out);
  nand nand_215 (nand_215_out, nand_214_out, and_12_out, nand_216_out);
  nand nand_216 (nand_216_out, nand_215_out, undriven[5]);
  nand nand_217 (nand_217_out, nand_220_out, nand_218_out);
  nand nand_218 (nand_218_out, nand_217_out, and_12_out);
  nand nand_219 (nand_219_out, nand_218_out, and_12_out, nand_220_out);
  nand nand_220 (nand_220_out, nand_219_out, undriven[3]);
  nand nand_221 (nand_221_out, nand_224_out, nand_222_out);
  nand nand_222 (nand_222_out, nand_221_out, and_12_out);
  nand nand_223 (nand_223_out, nand_222_out, and_12_out, nand_224_out);
  nand nand_224 (nand_224_out, nand_223_out, undriven[1]);
  nand nand_225 (nand_225_out, nand_228_out, nand_226_out);
  nand nand_226 (nand_226_out, nand_225_out, and_9_out);
  nand nand_227 (nand_227_out, nand_226_out, and_9_out, nand_228_out);
  nand nand_228 (nand_228_out, nand_227_out, undriven[7]);
  nand nand_229 (nand_229_out, nand_232_out, nand_230_out);
  nand nand_230 (nand_230_out, nand_229_out, and_9_out);
  nand nand_231 (nand_231_out, nand_230_out, and_9_out, nand_232_out);
  nand nand_232 (nand_232_out, nand_231_out, undriven[5]);
  nand nand_233 (nand_233_out, nand_236_out, nand_234_out);
  nand nand_234 (nand_234_out, nand_233_out, and_9_out);
  nand nand_235 (nand_235_out, nand_234_out, and_9_out, nand_236_out);
  nand nand_236 (nand_236_out, nand_235_out, undriven[3]);
  nand nand_237 (nand_237_out, nand_240_out, nand_238_out);
  nand nand_238 (nand_238_out, nand_237_out, and_9_out);
  nand nand_239 (nand_239_out, nand_238_out, and_9_out, nand_240_out);
  nand nand_240 (nand_240_out, nand_239_out, undriven[1]);
  nand nand_241 (nand_241_out, nand_146_out, nand_242_out);
  nand nand_242 (nand_242_out, nand_241_out, nand_147_out);
  and and_155 (and_76_out[7], nand_241_out, and_74_out);
  and and_156 (and_75_out[7], nand_241_out, and_50_out);
  nand nand_243 (nand_243_out, nand_150_out, nand_244_out);
  nand nand_244 (nand_244_out, nand_243_out, nand_151_out);
  and and_157 (and_76_out[5], nand_243_out, and_74_out);
  and and_158 (and_75_out[5], nand_243_out, and_50_out);
  nand nand_245 (nand_245_out, nand_154_out, nand_246_out);
  nand nand_246 (nand_246_out, nand_245_out, nand_155_out);
  and and_159 (and_76_out[3], nand_245_out, and_74_out);
  and and_160 (and_75_out[3], nand_245_out, and_50_out);
  nand nand_247 (nand_247_out, nand_158_out, nand_248_out);
  nand nand_248 (nand_248_out, nand_247_out, nand_159_out);
  and and_161 (and_76_out[1], nand_247_out, and_74_out);
  and and_162 (and_75_out[1], nand_247_out, and_50_out);
  nand nand_249 (nand_249_out, nand_162_out, nand_250_out);
  nand nand_250 (nand_250_out, nand_249_out, nand_163_out);
  and and_163 (and_76_out[7], nand_249_out, and_71_out);
  and and_164 (and_75_out[7], nand_249_out, and_47_out);
  nand nand_251 (nand_251_out, nand_166_out, nand_252_out);
  nand nand_252 (nand_252_out, nand_251_out, nand_167_out);
  and and_165 (and_76_out[5], nand_251_out, and_71_out);
  and and_166 (and_75_out[5], nand_251_out, and_47_out);
  nand nand_253 (nand_253_out, nand_170_out, nand_254_out);
  nand nand_254 (nand_254_out, nand_253_out, nand_171_out);
  and and_167 (and_76_out[3], nand_253_out, and_71_out);
  and and_168 (and_75_out[3], nand_253_out, and_47_out);
  nand nand_255 (nand_255_out, nand_174_out, nand_256_out);
  nand nand_256 (nand_256_out, nand_255_out, nand_175_out);
  and and_169 (and_76_out[1], nand_255_out, and_71_out);
  and and_170 (and_75_out[1], nand_255_out, and_47_out);
  nand nand_257 (nand_257_out, nand_178_out, nand_258_out);
  nand nand_258 (nand_258_out, nand_257_out, nand_179_out);
  and and_171 (and_76_out[7], nand_257_out, and_66_out);
  and and_172 (and_75_out[7], nand_257_out, and_44_out);
  nand nand_259 (nand_259_out, nand_182_out, nand_260_out);
  nand nand_260 (nand_260_out, nand_259_out, nand_183_out);
  and and_173 (and_76_out[5], nand_259_out, and_66_out);
  and and_174 (and_75_out[5], nand_259_out, and_44_out);
  nand nand_261 (nand_261_out, nand_186_out, nand_262_out);
  nand nand_262 (nand_262_out, nand_261_out, nand_187_out);
  and and_175 (and_76_out[3], nand_261_out, and_66_out);
  and and_176 (and_75_out[3], nand_261_out, and_44_out);
  nand nand_263 (nand_263_out, nand_190_out, nand_264_out);
  nand nand_264 (nand_264_out, nand_263_out, nand_191_out);
  and and_177 (and_76_out[1], nand_263_out, and_66_out);
  and and_178 (and_75_out[1], nand_263_out, and_44_out);
  nand nand_265 (nand_265_out, nand_194_out, nand_266_out);
  nand nand_266 (nand_266_out, nand_265_out, nand_195_out);
  and and_179 (and_76_out[7], nand_265_out, and_67_out);
  and and_180 (and_75_out[7], nand_265_out, and_40_out);
  nand nand_267 (nand_267_out, nand_198_out, nand_268_out);
  nand nand_268 (nand_268_out, nand_267_out, nand_199_out);
  and and_181 (and_76_out[5], nand_267_out, and_67_out);
  and and_182 (and_75_out[5], nand_267_out, and_40_out);
  nand nand_269 (nand_269_out, nand_202_out, nand_270_out);
  nand nand_270 (nand_270_out, nand_269_out, nand_203_out);
  and and_183 (and_76_out[3], nand_269_out, and_67_out);
  and and_184 (and_75_out[3], nand_269_out, and_40_out);
  nand nand_271 (nand_271_out, nand_206_out, nand_272_out);
  nand nand_272 (nand_272_out, nand_271_out, nand_207_out);
  and and_185 (and_76_out[1], nand_271_out, and_67_out);
  and and_186 (and_75_out[1], nand_271_out, and_40_out);
  nand nand_273 (nand_273_out, nand_210_out, nand_274_out);
  nand nand_274 (nand_274_out, nand_273_out, nand_211_out);
  and and_187 (and_76_out[7], nand_273_out, and_62_out);
  and and_188 (and_75_out[7], nand_273_out, and_34_out);
  nand nand_275 (nand_275_out, nand_214_out, nand_276_out);
  nand nand_276 (nand_276_out, nand_275_out, nand_215_out);
  and and_189 (and_76_out[5], nand_275_out, and_62_out);
  and and_190 (and_75_out[5], nand_275_out, and_34_out);
  nand nand_277 (nand_277_out, nand_218_out, nand_278_out);
  nand nand_278 (nand_278_out, nand_277_out, nand_219_out);
  and and_191 (and_76_out[3], nand_277_out, and_62_out);
  and and_192 (and_75_out[3], nand_277_out, and_34_out);
  nand nand_279 (nand_279_out, nand_222_out, nand_280_out);
  nand nand_280 (nand_280_out, nand_279_out, nand_223_out);
  and and_193 (and_76_out[1], nand_279_out, and_62_out);
  and and_194 (and_75_out[1], nand_279_out, and_34_out);
  nand nand_281 (nand_281_out, nand_226_out, nand_282_out);
  nand nand_282 (nand_282_out, nand_281_out, nand_227_out);
  and and_195 (and_76_out[7], nand_281_out, and_59_out);
  and and_196 (and_75_out[7], nand_281_out, and_35_out);
  nand nand_283 (nand_283_out, nand_230_out, nand_284_out);
  nand nand_284 (nand_284_out, nand_283_out, nand_231_out);
  and and_197 (and_76_out[5], nand_283_out, and_59_out);
  and and_198 (and_75_out[5], nand_283_out, and_35_out);
  nand nand_285 (nand_285_out, nand_234_out, nand_286_out);
  nand nand_286 (nand_286_out, nand_285_out, nand_235_out);
  and and_199 (and_76_out[3], nand_285_out, and_59_out);
  and and_200 (and_75_out[3], nand_285_out, and_35_out);
  nand nand_287 (nand_287_out, nand_238_out, nand_288_out);
  nand nand_288 (nand_288_out, nand_287_out, nand_239_out);
  and and_201 (and_76_out[1], nand_287_out, and_59_out);
  and and_202 (and_75_out[1], nand_287_out, and_35_out);
  DipSwitch dipswitch_1 (.out(dipswitch_1_out));
  and and_203 (and_218_out[0], dipswitch_1_out, 1'b0);
  and and_204 (and_218_out[1], dipswitch_1_out, 1'b0);
  and and_205 (and_218_out[2], dipswitch_1_out, 1'b0);
  // And and_206 has open pins: In_1=and_207_out, In_2=nand_335_out[7], out=open
  xor xor_1 (xor_8_out[7], nand_335_out[7], and_207_out);
  and and_207 (and_207_out, and_208_out, nand_335_out[6]);
  xor xor_2 (xor_8_out[6], nand_335_out[6], and_208_out);
  and and_208 (and_208_out, and_209_out, nand_335_out[5]);
  xor xor_3 (xor_8_out[5], nand_335_out[5], and_209_out);
  and and_209 (and_209_out, and_210_out, nand_335_out[4]);
  xor xor_4 (xor_8_out[4], nand_335_out[4], and_210_out);
  and and_210 (and_210_out, and_211_out, nand_335_out[3]);
  xor xor_5 (xor_8_out[3], nand_335_out[3], and_211_out);
  and and_211 (and_211_out, and_212_out, nand_335_out[2]);
  xor xor_6 (xor_8_out[2], nand_335_out[2], and_212_out);
  and and_212 (and_212_out, and_213_out, nand_335_out[1]);
  xor xor_7 (xor_8_out[1], nand_335_out[1], and_213_out);
  and and_213 (and_213_out, 1'b1, nand_335_out[0]);
  xor xor_8 (xor_8_out[0], nand_335_out[0], 1'b1);
  and and_214 (and_218_out[3], dipswitch_1_out, 1'b0);
  and and_215 (and_218_out[4], dipswitch_1_out, 1'b0);
  and and_216 (and_218_out[5], dipswitch_1_out, 1'b0);
  and and_217 (and_218_out[6], dipswitch_1_out, 1'b0);
  not not_27 (not_27_out, dipswitch_1_out);
  and and_218 (and_218_out[7], dipswitch_1_out, 1'b0);
  or or_1 (or_8_out[0], and_226_out[0], and_218_out[0]);
  or or_2 (or_8_out[1], and_226_out[1], and_218_out[1]);
  or or_3 (or_8_out[2], and_226_out[2], and_218_out[2]);
  and and_219 (and_226_out[0], not_27_out, xor_8_out[0]);
  and and_220 (and_226_out[1], not_27_out, xor_8_out[1]);
  and and_221 (and_226_out[2], not_27_out, xor_8_out[2]);
  and and_222 (and_226_out[3], not_27_out, xor_8_out[3]);
  and and_223 (and_226_out[4], not_27_out, xor_8_out[4]);
  and and_224 (and_226_out[5], not_27_out, xor_8_out[5]);
  and and_225 (and_226_out[6], not_27_out, xor_8_out[6]);
  and and_226 (and_226_out[7], not_27_out, xor_8_out[7]);
  or or_4 (or_8_out[3], and_226_out[3], and_218_out[3]);
  or or_5 (or_8_out[4], and_226_out[4], and_218_out[4]);
  or or_6 (or_8_out[5], and_226_out[5], and_218_out[5]);
  or or_7 (or_8_out[6], and_226_out[6], and_218_out[6]);
  or or_8 (or_8_out[7], and_226_out[7], and_218_out[7]);
  nand nand_289 (nand_289_out, nand_292_out, nand_290_out);
  nand nand_290 (nand_290_out, nand_289_out, clk);
  nand nand_291 (nand_291_out, nand_290_out, clk, nand_292_out);
  nand nand_292 (nand_292_out, nand_291_out, or_8_out[6]);
  nand nand_293 (nand_293_out, nand_296_out, nand_294_out);
  nand nand_294 (nand_294_out, nand_293_out, clk);
  nand nand_295 (nand_295_out, nand_294_out, clk, nand_296_out);
  nand nand_296 (nand_296_out, nand_295_out, or_8_out[4]);
  nand nand_297 (nand_297_out, nand_300_out, nand_298_out);
  nand nand_298 (nand_298_out, nand_297_out, clk);
  nand nand_299 (nand_299_out, nand_298_out, clk, nand_300_out);
  nand nand_300 (nand_300_out, nand_299_out, or_8_out[2]);
  nand nand_301 (nand_301_out, nand_304_out, nand_302_out);
  nand nand_302 (nand_302_out, nand_301_out, clk);
  nand nand_303 (nand_303_out, nand_302_out, clk, nand_304_out);
  nand nand_304 (nand_304_out, nand_303_out, or_8_out[0]);
  nand nand_305 (nand_335_out[6], nand_290_out, nand_306_out);
  nand nand_306 (nand_306_out, nand_335_out[6], nand_291_out);
  nand nand_307 (nand_335_out[4], nand_294_out, nand_308_out);
  nand nand_308 (nand_308_out, nand_335_out[4], nand_295_out);
  nand nand_309 (nand_335_out[2], nand_298_out, nand_310_out);
  nand nand_310 (nand_310_out, nand_335_out[2], nand_299_out);
  nand nand_311 (nand_335_out[0], nand_302_out, nand_312_out);
  nand nand_312 (nand_312_out, nand_335_out[0], nand_303_out);
  and and_227 (and_227_out, nand_335_out[6], 1'b0);
  and and_228 (and_228_out, nand_335_out[4], 1'b0);
  and and_229 (and_229_out, nand_335_out[2], 1'b0);
  and and_230 (and_230_out, nand_335_out[0], 1'b0);
  nand nand_313 (nand_313_out, nand_316_out, nand_314_out);
  nand nand_314 (nand_314_out, nand_313_out, clk);
  nand nand_315 (nand_315_out, nand_314_out, clk, nand_316_out);
  nand nand_316 (nand_316_out, nand_315_out, or_8_out[7]);
  nand nand_317 (nand_317_out, nand_320_out, nand_318_out);
  nand nand_318 (nand_318_out, nand_317_out, clk);
  nand nand_319 (nand_319_out, nand_318_out, clk, nand_320_out);
  nand nand_320 (nand_320_out, nand_319_out, or_8_out[5]);
  nand nand_321 (nand_321_out, nand_324_out, nand_322_out);
  nand nand_322 (nand_322_out, nand_321_out, clk);
  nand nand_323 (nand_323_out, nand_322_out, clk, nand_324_out);
  nand nand_324 (nand_324_out, nand_323_out, or_8_out[3]);
  nand nand_325 (nand_325_out, nand_328_out, nand_326_out);
  nand nand_326 (nand_326_out, nand_325_out, clk);
  nand nand_327 (nand_327_out, nand_326_out, clk, nand_328_out);
  nand nand_328 (nand_328_out, nand_327_out, or_8_out[1]);
  nand nand_329 (nand_335_out[7], nand_314_out, nand_330_out);
  nand nand_330 (nand_330_out, nand_335_out[7], nand_315_out);
  and and_231 (and_231_out, nand_335_out[7], 1'b0);
  nand nand_331 (nand_335_out[5], nand_318_out, nand_332_out);
  nand nand_332 (nand_332_out, nand_335_out[5], nand_319_out);
  and and_232 (and_232_out, nand_335_out[5], 1'b0);
  nand nand_333 (nand_335_out[3], nand_322_out, nand_334_out);
  nand nand_334 (nand_334_out, nand_335_out[3], nand_323_out);
  and and_233 (and_233_out, nand_335_out[3], 1'b0);
  nand nand_335 (nand_335_out[1], nand_326_out, nand_336_out);
  nand nand_336 (nand_336_out, nand_335_out[1], nand_327_out);
  and and_234 (and_234_out, nand_335_out[1], 1'b0);
  not not_28 (not_28_out, In_3);
  not not_29 (not_29_out, In_2);
  not not_30 (not_30_out, In_1);
  not not_31 (not_31_out, In_3);
  not not_32 (not_32_out, In_2);
  not not_33 (not_33_out, In_1);
  not not_34 (not_34_out, not_28_out);
  and and_235 (and_235_out, not_30_out, not_29_out);
  and and_236 (and_236_out, In_1, not_29_out);
  and and_237 (and_237_out, not_30_out, In_2);
  and and_238 (and_238_out, In_2, In_1);
  and and_239 (and_239_out, not_33_out, not_32_out);
  and and_240 (and_240_out, In_1, not_32_out);
  and and_241 (and_241_out, not_33_out, In_2);
  and and_242 (and_242_out, In_2, In_1);
  and and_243 (and_243_out, and_235_out, not_31_out);
  and and_244 (and_244_out, and_236_out, not_31_out);
  and and_245 (and_245_out, and_237_out, not_31_out);
  and and_246 (and_246_out, and_238_out, not_31_out);
  and and_247 (and_247_out, and_239_out, not_34_out);
  and and_248 (and_248_out, and_240_out, not_34_out);
  and and_249 (and_249_out, and_241_out, not_34_out);
  // And and_250 has open pins: In_1=and_242_out, In_2=not_34_out, out=open
  or or_9 (or_9_out, Num_1[7], Num_1[6]);
  or or_10 (or_10_out, Num_1[5], Num_1[4]);
  or or_11 (or_11_out, Num_1[3], Num_1[2]);
  or or_12 (or_12_out, Num_1[1], Num_1[0]);
  or or_13 (or_13_out, or_9_out, or_10_out);
  or or_14 (or_14_out, or_13_out, or_15_out);
  or or_15 (or_15_out, or_11_out, or_12_out);
  or or_16 (or_16_out, and_248_out, or_17_out);
  or or_17 (or_17_out, and_247_out, and_243_out);
  or or_18 (or_18_out, and_249_out, or_19_out);
  or or_19 (or_19_out, and_253_out, or_23_out);
  or or_20 (or_20_out, or_19_out, or_18_out);
  or or_21 (or_21_out, and_245_out, and_247_out);
  or or_22 (or_22_out, and_246_out, and_248_out);
  or or_23 (or_23_out, and_252_out, or_25_out);
  or or_24 (Out_0, or_26_out, or_20_out);
  not not_35 (not_35_out, or_14_out);
  not not_36 (not_36_out, Num_1[7]);
  or or_25 (or_25_out, and_251_out, and_254_out);
  or or_26 (or_26_out, or_25_out, or_23_out);
  and and_251 (and_251_out, or_16_out, not_35_out);
  and and_252 (and_252_out, or_14_out, and_244_out);
  and and_253 (and_253_out, or_21_out, not_36_out);
  and and_254 (and_254_out, Num_1[7], or_22_out);
  xor xor_9 (xor_9_out, B_0[7], and_334_out);
  xor xor_10 (xor_10_out, B_0[6], and_334_out);
  xor xor_11 (xor_11_out, B_0[5], and_334_out);
  xor xor_12 (xor_12_out, B_0[4], and_334_out);
  xor xor_13 (xor_13_out, B_0[3], and_334_out);
  xor xor_14 (xor_14_out, B_0[2], and_334_out);
  xor xor_15 (xor_15_out, B_0[1], and_334_out);
  xor xor_16 (xor_16_out, B_0[0], and_334_out);
  and and_255 (and_274_out[0], B_0[0], A_0[0]);
  nand nand_337 (nand_344_out[0], B_0[0], A_0[0]);
  or or_27 (or_42_out[0], B_0[0], A_0[0]);
  nor nor_1 (nor_8_out[0], B_0[0], A_0[0]);
  xor xor_17 (xor_36_out[0], B_0[0], A_0[0]);
  and and_256 (and_274_out[1], B_0[1], A_0[1]);
  nand nand_338 (nand_344_out[1], B_0[1], A_0[1]);
  or or_28 (or_42_out[1], B_0[1], A_0[1]);
  nor nor_2 (nor_8_out[1], B_0[1], A_0[1]);
  xor xor_18 (xor_36_out[1], B_0[1], A_0[1]);
  and and_257 (and_274_out[2], B_0[2], A_0[2]);
  nand nand_339 (nand_344_out[2], B_0[2], A_0[2]);
  or or_29 (or_42_out[2], B_0[2], A_0[2]);
  nor nor_3 (nor_8_out[2], B_0[2], A_0[2]);
  xor xor_19 (xor_36_out[2], B_0[2], A_0[2]);
  and and_258 (and_274_out[3], B_0[3], A_0[3]);
  and and_259 (and_274_out[4], B_0[4], A_0[4]);
  nand nand_340 (nand_344_out[3], B_0[3], A_0[3]);
  nand nand_341 (nand_344_out[4], B_0[4], A_0[4]);
  or or_30 (or_42_out[3], B_0[3], A_0[3]);
  or or_31 (or_42_out[4], B_0[4], A_0[4]);
  nor nor_4 (nor_8_out[3], B_0[3], A_0[3]);
  nor nor_5 (nor_8_out[4], B_0[4], A_0[4]);
  xor xor_20 (xor_36_out[3], B_0[3], A_0[3]);
  xor xor_21 (xor_36_out[4], B_0[4], A_0[4]);
  and and_260 (and_274_out[5], B_0[5], A_0[5]);
  nand nand_342 (nand_344_out[5], B_0[5], A_0[5]);
  or or_32 (or_42_out[5], B_0[5], A_0[5]);
  nor nor_6 (nor_8_out[5], B_0[5], A_0[5]);
  xor xor_22 (xor_36_out[5], B_0[5], A_0[5]);
  and and_261 (and_261_out, xor_9_out, A_0[7]);
  xor xor_23 (xor_23_out, A_0[7], xor_9_out);
  and and_262 (and_262_out, xor_10_out, A_0[6]);
  xor xor_24 (xor_24_out, A_0[6], xor_10_out);
  and and_263 (and_263_out, xor_11_out, A_0[5]);
  xor xor_25 (xor_25_out, A_0[5], xor_11_out);
  and and_264 (and_264_out, xor_12_out, A_0[4]);
  xor xor_26 (xor_26_out, A_0[4], xor_12_out);
  and and_265 (and_265_out, xor_13_out, A_0[3]);
  xor xor_27 (xor_27_out, A_0[3], xor_13_out);
  and and_266 (and_266_out, xor_14_out, A_0[2]);
  xor xor_28 (xor_28_out, A_0[2], xor_14_out);
  and and_267 (and_267_out, xor_15_out, A_0[1]);
  xor xor_29 (xor_29_out, A_0[1], xor_15_out);
  and and_268 (and_268_out, xor_16_out, A_0[0]);
  xor xor_30 (xor_30_out, A_0[0], xor_16_out);
  and and_269 (and_274_out[6], B_0[6], A_0[6]);
  nand nand_343 (nand_344_out[6], B_0[6], A_0[6]);
  or or_33 (or_42_out[6], B_0[6], A_0[6]);
  nor nor_7 (nor_8_out[6], B_0[6], A_0[6]);
  xor xor_31 (xor_36_out[6], B_0[6], A_0[6]);
  or or_34 (or_34_out, and_261_out, and_270_out);
  and and_270 (and_270_out, xor_23_out, or_35_out);
  xor xor_32 (xor_40_out[7], xor_23_out, or_35_out);
  or or_35 (or_35_out, and_262_out, and_271_out);
  and and_271 (and_271_out, xor_24_out, or_36_out);
  xor xor_33 (xor_40_out[6], xor_24_out, or_36_out);
  or or_36 (or_36_out, and_263_out, and_272_out);
  and and_272 (and_272_out, xor_25_out, or_37_out);
  xor xor_34 (xor_40_out[5], xor_25_out, or_37_out);
  or or_37 (or_37_out, and_264_out, and_273_out);
  and and_273 (and_273_out, xor_26_out, or_38_out);
  xor xor_35 (xor_40_out[4], xor_26_out, or_38_out);
  or or_38 (or_38_out, and_265_out, and_275_out);
  or or_39 (or_39_out, and_266_out, and_276_out);
  or or_40 (or_40_out, and_267_out, and_277_out);
  or or_41 (or_41_out, and_268_out, and_278_out);
  and and_274 (and_274_out[7], B_0[7], A_0[7]);
  nand nand_344 (nand_344_out[7], B_0[7], A_0[7]);
  or or_42 (or_42_out[7], B_0[7], A_0[7]);
  nor nor_8 (nor_8_out[7], B_0[7], A_0[7]);
  xor xor_36 (xor_36_out[7], B_0[7], A_0[7]);
  and and_275 (and_275_out, xor_27_out, or_39_out);
  xor xor_37 (xor_40_out[3], xor_27_out, or_39_out);
  and and_276 (and_276_out, xor_28_out, or_40_out);
  xor xor_38 (xor_40_out[2], xor_28_out, or_40_out);
  and and_277 (and_277_out, xor_29_out, or_41_out);
  xor xor_39 (xor_40_out[1], xor_29_out, or_41_out);
  and and_278 (and_278_out, xor_30_out, and_334_out);
  xor xor_40 (xor_40_out[0], xor_30_out, and_334_out);
  and and_279 (and_314_out[0], and_335_out, and_274_out[0]);
  and and_280 (and_314_out[1], and_335_out, and_274_out[1]);
  and and_281 (and_315_out[0], and_336_out, nand_344_out[0]);
  and and_282 (and_315_out[1], and_336_out, nand_344_out[1]);
  and and_283 (and_316_out[0], and_337_out, or_42_out[0]);
  and and_284 (and_316_out[1], and_337_out, or_42_out[1]);
  and and_285 (and_317_out[0], and_338_out, nor_8_out[0]);
  and and_286 (and_317_out[1], and_338_out, nor_8_out[1]);
  and and_287 (and_318_out[0], and_339_out, xor_36_out[0]);
  and and_288 (and_318_out[1], and_339_out, xor_36_out[1]);
  and and_289 (and_314_out[2], and_335_out, and_274_out[2]);
  and and_290 (and_315_out[2], and_336_out, nand_344_out[2]);
  and and_291 (and_316_out[2], and_337_out, or_42_out[2]);
  and and_292 (and_317_out[2], and_338_out, nor_8_out[2]);
  and and_293 (and_318_out[2], and_339_out, xor_36_out[2]);
  and and_294 (and_314_out[3], and_335_out, and_274_out[3]);
  and and_295 (and_315_out[3], and_336_out, nand_344_out[3]);
  and and_296 (and_316_out[3], and_337_out, or_42_out[3]);
  and and_297 (and_317_out[3], and_338_out, nor_8_out[3]);
  and and_298 (and_318_out[3], and_339_out, xor_36_out[3]);
  and and_299 (and_314_out[4], and_335_out, and_274_out[4]);
  and and_300 (and_314_out[5], and_335_out, and_274_out[5]);
  and and_301 (and_315_out[4], and_336_out, nand_344_out[4]);
  and and_302 (and_315_out[5], and_336_out, nand_344_out[5]);
  and and_303 (and_316_out[4], and_337_out, or_42_out[4]);
  and and_304 (and_316_out[5], and_337_out, or_42_out[5]);
  and and_305 (and_317_out[4], and_338_out, nor_8_out[4]);
  and and_306 (and_317_out[5], and_338_out, nor_8_out[5]);
  and and_307 (and_318_out[4], and_339_out, xor_36_out[4]);
  and and_308 (and_318_out[5], and_339_out, xor_36_out[5]);
  and and_309 (and_314_out[6], and_335_out, and_274_out[6]);
  and and_310 (and_315_out[6], and_336_out, nand_344_out[6]);
  and and_311 (and_316_out[6], and_337_out, or_42_out[6]);
  and and_312 (and_317_out[6], and_338_out, nor_8_out[6]);
  and and_313 (and_318_out[6], and_339_out, xor_36_out[6]);
  and and_314 (and_314_out[7], and_335_out, and_274_out[7]);
  and and_315 (and_315_out[7], and_336_out, nand_344_out[7]);
  and and_316 (and_316_out[7], and_337_out, or_42_out[7]);
  and and_317 (and_317_out[7], and_338_out, nor_8_out[7]);
  and and_318 (and_318_out[7], and_339_out, xor_36_out[7]);
  not not_37 (not_37_out, C_2);
  and and_319 (and_342_out[0], or_43_out, xor_40_out[0]);
  not not_38 (not_38_out, C_1);
  not not_39 (not_39_out, C_1);
  and and_320 (and_342_out[1], or_43_out, xor_40_out[1]);
  not not_40 (not_40_out, C_0);
  and and_321 (and_321_out, not_40_out, not_38_out);
  and and_322 (and_322_out, C_0, not_38_out);
  and and_323 (and_323_out, not_40_out, C_1);
  and and_324 (and_324_out, C_1, C_0);
  not not_41 (not_41_out, C_2);
  not not_42 (not_42_out, C_0);
  and and_325 (and_325_out, not_42_out, not_39_out);
  and and_326 (and_326_out, C_0, not_39_out);
  and and_327 (and_327_out, not_42_out, C_1);
  and and_328 (and_328_out, C_1, C_0);
  not not_43 (not_43_out, not_37_out);
  and and_329 (and_342_out[2], or_43_out, xor_40_out[2]);
  and and_330 (and_342_out[3], or_43_out, xor_40_out[3]);
  and and_331 (and_342_out[4], or_43_out, xor_40_out[4]);
  // And and_332 has open pins: In_1=and_321_out, In_2=not_41_out, out=open
  and and_333 (and_333_out, and_322_out, not_41_out);
  and and_334 (and_334_out, and_323_out, not_41_out);
  and and_335 (and_335_out, and_324_out, not_41_out);
  and and_336 (and_336_out, and_325_out, not_43_out);
  and and_337 (and_337_out, and_326_out, not_43_out);
  and and_338 (and_338_out, and_327_out, not_43_out);
  and and_339 (and_339_out, and_328_out, not_43_out);
  and and_340 (and_342_out[5], or_43_out, xor_40_out[5]);
  and and_341 (and_342_out[6], or_43_out, xor_40_out[6]);
  DipSwitch dipswitch_2 (.out(dipswitch_2_out));
  DipSwitch dipswitch_3 (.out(dipswitch_3_out));
  DipSwitch dipswitch_4 (.out(dipswitch_4_out));
  and and_342 (and_342_out[7], or_43_out, xor_40_out[7]);
  or or_43 (or_43_out, and_333_out, and_334_out);
  or or_44 (O_0[0], and_342_out[0], or_80_out[0]);
  or or_45 (or_80_out[0], and_314_out[0], or_81_out[0]);
  or or_46 (or_81_out[0], and_315_out[0], or_82_out[0]);
  or or_47 (or_82_out[0], and_316_out[0], or_83_out[0]);
  or or_48 (or_83_out[0], and_317_out[0], and_318_out[0]);
  nand nand_345 (nand_345_out, nand_348_out, nand_346_out);
  nand nand_346 (nand_346_out, nand_345_out, dipswitch_2_out);
  nand nand_347 (nand_347_out, nand_346_out, dipswitch_2_out, nand_348_out);
  nand nand_348 (nand_348_out, nand_347_out, in_13[6]);
  nand nand_349 (nand_349_out, nand_352_out, nand_350_out);
  nand nand_350 (nand_350_out, nand_349_out, dipswitch_2_out);
  nand nand_351 (nand_351_out, nand_350_out, dipswitch_2_out, nand_352_out);
  nand nand_352 (nand_352_out, nand_351_out, in_13[4]);
  nand nand_353 (nand_353_out, nand_356_out, nand_354_out);
  nand nand_354 (nand_354_out, nand_353_out, dipswitch_2_out);
  nand nand_355 (nand_355_out, nand_354_out, dipswitch_2_out, nand_356_out);
  nand nand_356 (nand_356_out, nand_355_out, in_13[2]);
  nand nand_357 (nand_357_out, nand_360_out, nand_358_out);
  nand nand_358 (nand_358_out, nand_357_out, dipswitch_2_out);
  nand nand_359 (nand_359_out, nand_358_out, dipswitch_2_out, nand_360_out);
  nand nand_360 (nand_360_out, nand_359_out, in_13[0]);
  or or_49 (O_0[1], and_342_out[1], or_80_out[1]);
  or or_50 (or_80_out[1], and_314_out[1], or_81_out[1]);
  or or_51 (or_81_out[1], and_315_out[1], or_82_out[1]);
  or or_52 (or_82_out[1], and_316_out[1], or_83_out[1]);
  or or_53 (or_83_out[1], and_317_out[1], and_318_out[1]);
  or or_54 (O_0[2], and_342_out[2], or_80_out[2]);
  or or_55 (or_80_out[2], and_314_out[2], or_81_out[2]);
  or or_56 (or_81_out[2], and_315_out[2], or_82_out[2]);
  or or_57 (or_82_out[2], and_316_out[2], or_83_out[2]);
  or or_58 (or_83_out[2], and_317_out[2], and_318_out[2]);
  or or_59 (O_0[3], and_342_out[3], or_80_out[3]);
  or or_60 (O_0[4], and_342_out[4], or_80_out[4]);
  or or_61 (or_80_out[3], and_314_out[3], or_81_out[3]);
  or or_62 (or_80_out[4], and_314_out[4], or_81_out[4]);
  or or_63 (or_81_out[3], and_315_out[3], or_82_out[3]);
  or or_64 (or_81_out[4], and_315_out[4], or_82_out[4]);
  or or_65 (or_82_out[3], and_316_out[3], or_83_out[3]);
  or or_66 (or_82_out[4], and_316_out[4], or_83_out[4]);
  or or_67 (or_83_out[3], and_317_out[3], and_318_out[3]);
  or or_68 (or_83_out[4], and_317_out[4], and_318_out[4]);
  nand nand_361 (nand_361_out, nand_346_out, nand_362_out);
  nand nand_362 (nand_362_out, nand_361_out, nand_347_out);
  and and_343 (and_343_out, nand_361_out, dipswitch_3_out);
  and and_344 (and_344_out, nand_361_out, dipswitch_4_out);
  nand nand_363 (nand_363_out, nand_350_out, nand_364_out);
  nand nand_364 (nand_364_out, nand_363_out, nand_351_out);
  and and_345 (and_345_out, nand_363_out, dipswitch_3_out);
  and and_346 (and_346_out, nand_363_out, dipswitch_4_out);
  nand nand_365 (nand_365_out, nand_354_out, nand_366_out);
  nand nand_366 (nand_366_out, nand_365_out, nand_355_out);
  and and_347 (and_347_out, nand_365_out, dipswitch_3_out);
  and and_348 (and_348_out, nand_365_out, dipswitch_4_out);
  nand nand_367 (nand_367_out, nand_358_out, nand_368_out);
  nand nand_368 (nand_368_out, nand_367_out, nand_359_out);
  and and_349 (and_349_out, nand_367_out, dipswitch_3_out);
  and and_350 (and_350_out, nand_367_out, dipswitch_4_out);
  or or_69 (O_0[5], and_342_out[5], or_80_out[5]);
  or or_70 (or_80_out[5], and_314_out[5], or_81_out[5]);
  or or_71 (or_81_out[5], and_315_out[5], or_82_out[5]);
  or or_72 (or_82_out[5], and_316_out[5], or_83_out[5]);
  or or_73 (or_83_out[5], and_317_out[5], and_318_out[5]);
  or or_74 (O_0[6], and_342_out[6], or_80_out[6]);
  or or_75 (or_80_out[6], and_314_out[6], or_81_out[6]);
  or or_76 (or_81_out[6], and_315_out[6], or_82_out[6]);
  or or_77 (or_82_out[6], and_316_out[6], or_83_out[6]);
  or or_78 (or_83_out[6], and_317_out[6], and_318_out[6]);
  or or_79 (O_0[7], and_342_out[7], or_80_out[7]);
  or or_80 (or_80_out[7], and_314_out[7], or_81_out[7]);
  or or_81 (or_81_out[7], and_315_out[7], or_82_out[7]);
  or or_82 (or_82_out[7], and_316_out[7], or_83_out[7]);
  or or_83 (or_83_out[7], and_317_out[7], and_318_out[7]);
  nand nand_369 (nand_369_out, nand_372_out, nand_370_out);
  nand nand_370 (nand_370_out, nand_369_out, dipswitch_2_out);
  nand nand_371 (nand_371_out, nand_370_out, dipswitch_2_out, nand_372_out);
  nand nand_372 (nand_372_out, nand_371_out, in_13[7]);
  nand nand_373 (nand_373_out, nand_376_out, nand_374_out);
  nand nand_374 (nand_374_out, nand_373_out, dipswitch_2_out);
  nand nand_375 (nand_375_out, nand_374_out, dipswitch_2_out, nand_376_out);
  nand nand_376 (nand_376_out, nand_375_out, in_13[5]);
  nand nand_377 (nand_377_out, nand_380_out, nand_378_out);
  nand nand_378 (nand_378_out, nand_377_out, dipswitch_2_out);
  nand nand_379 (nand_379_out, nand_378_out, dipswitch_2_out, nand_380_out);
  nand nand_380 (nand_380_out, nand_379_out, in_13[3]);
  nand nand_381 (nand_381_out, nand_384_out, nand_382_out);
  nand nand_382 (nand_382_out, nand_381_out, dipswitch_2_out);
  nand nand_383 (nand_383_out, nand_382_out, dipswitch_2_out, nand_384_out);
  nand nand_384 (nand_384_out, nand_383_out, in_13[1]);
  nand nand_385 (nand_385_out, nand_370_out, nand_386_out);
  nand nand_386 (nand_386_out, nand_385_out, nand_371_out);
  and and_351 (and_351_out, nand_385_out, dipswitch_3_out);
  and and_352 (and_352_out, nand_385_out, dipswitch_4_out);
  nand nand_387 (nand_387_out, nand_374_out, nand_388_out);
  nand nand_388 (nand_388_out, nand_387_out, nand_375_out);
  and and_353 (and_353_out, nand_387_out, dipswitch_3_out);
  and and_354 (and_354_out, nand_387_out, dipswitch_4_out);
  nand nand_389 (nand_389_out, nand_378_out, nand_390_out);
  nand nand_390 (nand_390_out, nand_389_out, nand_379_out);
  and and_355 (and_355_out, nand_389_out, dipswitch_3_out);
  and and_356 (and_356_out, nand_389_out, dipswitch_4_out);
  nand nand_391 (nand_391_out, nand_382_out, nand_392_out);
  nand nand_392 (nand_392_out, nand_391_out, nand_383_out);
  and and_357 (and_357_out, nand_391_out, dipswitch_3_out);
  and and_358 (and_358_out, nand_391_out, dipswitch_4_out);
  // NotConnected on notconnected_1_out
  // NotConnected on notconnected_2_out
  // NotConnected on notconnected_3_out
  // NotConnected on notconnected_4_out
  // NotConnected on notconnected_5_out
  // NotConnected on notconnected_6_out
  // NotConnected on notconnected_7_out
  // NotConnected on notconnected_8_out
  nand nand_393 (nand_393_out, nand_396_out, nand_394_out);
  nand nand_394 (nand_394_out, nand_393_out, notconnected_2_out);
  nand nand_395 (nand_395_out, nand_394_out, notconnected_2_out, nand_396_out);
  nand nand_396 (nand_396_out, nand_395_out, notconnected_1_out[6]);
  nand nand_397 (nand_397_out, nand_400_out, nand_398_out);
  nand nand_398 (nand_398_out, nand_397_out, notconnected_2_out);
  nand nand_399 (nand_399_out, nand_398_out, notconnected_2_out, nand_400_out);
  nand nand_400 (nand_400_out, nand_399_out, notconnected_1_out[4]);
  nand nand_401 (nand_401_out, nand_404_out, nand_402_out);
  nand nand_402 (nand_402_out, nand_401_out, notconnected_2_out);
  nand nand_403 (nand_403_out, nand_402_out, notconnected_2_out, nand_404_out);
  nand nand_404 (nand_404_out, nand_403_out, notconnected_1_out[2]);
  nand nand_405 (nand_405_out, nand_408_out, nand_406_out);
  nand nand_406 (nand_406_out, nand_405_out, notconnected_2_out);
  nand nand_407 (nand_407_out, nand_406_out, notconnected_2_out, nand_408_out);
  nand nand_408 (nand_408_out, nand_407_out, notconnected_1_out[0]);
  DipSwitch dipswitch_5 (.out(dipswitch_5_out));
  DipSwitch dipswitch_6 (.out(dipswitch_6_out));
  DipSwitch dipswitch_7 (.out(dipswitch_7_out));
  not not_44 (not_44_out, notconnected_6_out[7]);
  and and_359 (and_359_out, notconnected_4_out, notconnected_6_out[7]);
  not not_45 (not_45_out, notconnected_6_out[6]);
  and and_360 (and_360_out, notconnected_4_out, notconnected_6_out[6]);
  not not_46 (not_46_out, notconnected_6_out[5]);
  and and_361 (and_361_out, notconnected_4_out, notconnected_6_out[5]);
  not not_47 (not_47_out, notconnected_6_out[4]);
  and and_362 (and_362_out, notconnected_4_out, notconnected_6_out[4]);
  not not_48 (not_48_out, notconnected_6_out[3]);
  and and_363 (and_363_out, notconnected_4_out, notconnected_6_out[3]);
  not not_49 (not_49_out, notconnected_6_out[2]);
  and and_364 (and_364_out, notconnected_4_out, notconnected_6_out[2]);
  not not_50 (not_50_out, notconnected_6_out[1]);
  and and_365 (and_365_out, notconnected_4_out, notconnected_6_out[1]);
  not not_51 (not_51_out, notconnected_6_out[0]);
  and and_366 (and_366_out, notconnected_4_out, notconnected_6_out[0]);
  and and_367 (and_367_out, not_52_out, dipswitch_6_out);
  not not_52 (not_52_out, dipswitch_7_out);
  and and_368 (and_368_out, dipswitch_6_out, dipswitch_7_out);
  and and_369 (and_369_out, not_44_out, notconnected_4_out);
  and and_370 (and_370_out, not_45_out, notconnected_4_out);
  and and_371 (and_371_out, not_46_out, notconnected_4_out);
  and and_372 (and_372_out, not_47_out, notconnected_4_out);
  and and_373 (and_373_out, not_48_out, notconnected_4_out);
  and and_374 (and_374_out, not_49_out, notconnected_4_out);
  and and_375 (and_375_out, not_50_out, notconnected_4_out);
  and and_376 (and_376_out, not_51_out, notconnected_4_out);
  nor nor_9 (nor_9_out, and_369_out, nor_10_out);
  nor nor_10 (nor_10_out, nor_9_out, and_359_out);
  nor nor_11 (nor_11_out, and_370_out, nor_12_out);
  nor nor_12 (nor_12_out, nor_11_out, and_360_out);
  nor nor_13 (nor_13_out, and_371_out, nor_14_out);
  nor nor_14 (nor_14_out, nor_13_out, and_361_out);
  nor nor_15 (nor_15_out, and_372_out, nor_16_out);
  nor nor_16 (nor_16_out, nor_15_out, and_362_out);
  nor nor_17 (nor_17_out, and_373_out, nor_18_out);
  nor nor_18 (nor_18_out, nor_17_out, and_363_out);
  nor nor_19 (nor_19_out, and_374_out, nor_20_out);
  nor nor_20 (nor_20_out, nor_19_out, and_364_out);
  nor nor_21 (nor_21_out, and_375_out, nor_22_out);
  nor nor_22 (nor_22_out, nor_21_out, and_365_out);
  nor nor_23 (nor_23_out, and_376_out, nor_24_out);
  nor nor_24 (nor_24_out, nor_23_out, and_366_out);
  nand nand_409 (nand_409_out, nand_394_out, nand_410_out);
  nand nand_410 (nand_410_out, nand_409_out, nand_395_out);
  and and_377 (and_377_out, nand_409_out, notconnected_3_out);
  nand nand_411 (nand_411_out, nand_398_out, nand_412_out);
  nand nand_412 (nand_412_out, nand_411_out, nand_399_out);
  and and_378 (and_378_out, nand_411_out, notconnected_3_out);
  nand nand_413 (nand_413_out, nand_402_out, nand_414_out);
  nand nand_414 (nand_414_out, nand_413_out, nand_403_out);
  and and_379 (and_379_out, nand_413_out, notconnected_3_out);
  nand nand_415 (nand_415_out, nand_406_out, nand_416_out);
  nand nand_416 (nand_416_out, nand_415_out, nand_407_out);
  and and_380 (and_380_out, nand_415_out, notconnected_3_out);
  and and_381 (and_381_out, notconnected_7_out[7], notconnected_8_out[7]);
  xor xor_41 (xor_41_out, notconnected_8_out[7], notconnected_7_out[7]);
  and and_382 (and_382_out, notconnected_7_out[6], notconnected_8_out[6]);
  xor xor_42 (xor_42_out, notconnected_8_out[6], notconnected_7_out[6]);
  and and_383 (and_383_out, notconnected_7_out[5], notconnected_8_out[5]);
  xor xor_43 (xor_43_out, notconnected_8_out[5], notconnected_7_out[5]);
  and and_384 (and_384_out, notconnected_7_out[4], notconnected_8_out[4]);
  xor xor_44 (xor_44_out, notconnected_8_out[4], notconnected_7_out[4]);
  and and_385 (and_385_out, notconnected_7_out[3], notconnected_8_out[3]);
  xor xor_45 (xor_45_out, notconnected_8_out[3], notconnected_7_out[3]);
  and and_386 (and_386_out, notconnected_7_out[2], notconnected_8_out[2]);
  xor xor_46 (xor_46_out, notconnected_8_out[2], notconnected_7_out[2]);
  and and_387 (and_387_out, notconnected_7_out[1], notconnected_8_out[1]);
  xor xor_47 (xor_47_out, notconnected_8_out[1], notconnected_7_out[1]);
  and and_388 (and_388_out, notconnected_7_out[0], notconnected_8_out[0]);
  xor xor_48 (xor_48_out, notconnected_8_out[0], notconnected_7_out[0]);
  nor nor_25 (nor_25_out, and_367_out, nor_26_out);
  nor nor_26 (nor_26_out, nor_25_out, and_368_out);
  or or_84 (or_84_out, and_381_out, and_389_out);
  and and_389 (and_389_out, xor_41_out, or_85_out);
  xor xor_49 (xor_49_out, xor_41_out, or_85_out);
  or or_85 (or_85_out, and_382_out, and_390_out);
  and and_390 (and_390_out, xor_42_out, or_86_out);
  xor xor_50 (xor_50_out, xor_42_out, or_86_out);
  or or_86 (or_86_out, and_383_out, and_391_out);
  and and_391 (and_391_out, xor_43_out, or_87_out);
  xor xor_51 (xor_51_out, xor_43_out, or_87_out);
  or or_87 (or_87_out, and_384_out, and_392_out);
  and and_392 (and_392_out, xor_44_out, or_88_out);
  xor xor_52 (xor_52_out, xor_44_out, or_88_out);
  or or_88 (or_88_out, and_385_out, and_401_out);
  or or_89 (or_89_out, and_386_out, and_402_out);
  or or_90 (or_90_out, and_387_out, and_403_out);
  or or_91 (or_91_out, and_388_out, and_404_out);
  // NotConnected on notconnected_9_out
  Reset reset_1 ();  // open: out
  Reset reset_2 ();  // open: out
  and and_393 (and_393_out, nor_9_out, notconnected_5_out);
  Reset reset_3 ();  // open: out
  and and_394 (and_394_out, nor_11_out, notconnected_5_out);
  Reset reset_4 ();  // open: out
  and and_395 (and_395_out, nor_13_out, notconnected_5_out);
  Reset reset_5 ();  // open: out
  and and_396 (and_396_out, nor_15_out, notconnected_5_out);
  Reset reset_6 ();  // open: out
  and and_397 (and_397_out, nor_17_out, notconnected_5_out);
  Reset reset_7 ();  // open: out
  and and_398 (and_398_out, nor_19_out, notconnected_5_out);
  Reset reset_8 ();  // open: out
  and and_399 (and_399_out, nor_21_out, notconnected_5_out);
  Reset reset_9 ();  // open: out
  and and_400 (and_400_out, nor_23_out, notconnected_5_out);
  and and_401 (and_401_out, xor_45_out, or_89_out);
  xor xor_53 (xor_53_out, xor_45_out, or_89_out);
  and and_402 (and_402_out, xor_46_out, or_90_out);
  xor xor_54 (xor_54_out, xor_46_out, or_90_out);
  and and_403 (and_403_out, xor_47_out, or_91_out);
  xor xor_55 (xor_55_out, xor_47_out, or_91_out);
  and and_404 (and_404_out, xor_48_out, notconnected_9_out);
  xor xor_56 (xor_56_out, xor_48_out, notconnected_9_out);
  and and_405 (and_405_out, nor_25_out, dipswitch_5_out);
  nand nand_417 (nand_417_out, nand_420_out, nand_418_out);
  nand nand_418 (nand_418_out, nand_417_out, notconnected_2_out);
  nand nand_419 (nand_419_out, nand_418_out, notconnected_2_out, nand_420_out);
  nand nand_420 (nand_420_out, nand_419_out, notconnected_1_out[7]);
  nand nand_421 (nand_421_out, nand_424_out, nand_422_out);
  nand nand_422 (nand_422_out, nand_421_out, notconnected_2_out);
  nand nand_423 (nand_423_out, nand_422_out, notconnected_2_out, nand_424_out);
  nand nand_424 (nand_424_out, nand_423_out, notconnected_1_out[5]);
  nand nand_425 (nand_425_out, nand_428_out, nand_426_out);
  nand nand_426 (nand_426_out, nand_425_out, notconnected_2_out);
  nand nand_427 (nand_427_out, nand_426_out, notconnected_2_out, nand_428_out);
  nand nand_428 (nand_428_out, nand_427_out, notconnected_1_out[3]);
  nand nand_429 (nand_429_out, nand_432_out, nand_430_out);
  nand nand_430 (nand_430_out, nand_429_out, notconnected_2_out);
  nand nand_431 (nand_431_out, nand_430_out, notconnected_2_out, nand_432_out);
  nand nand_432 (nand_432_out, nand_431_out, notconnected_1_out[1]);
  nand nand_433 (nand_433_out, nand_418_out, nand_434_out);
  nand nand_434 (nand_434_out, nand_433_out, nand_419_out);
  and and_406 (and_406_out, nand_433_out, notconnected_3_out);
  nand nand_435 (nand_435_out, nand_422_out, nand_436_out);
  nand nand_436 (nand_436_out, nand_435_out, nand_423_out);
  and and_407 (and_407_out, nand_435_out, notconnected_3_out);
  nand nand_437 (nand_437_out, nand_426_out, nand_438_out);
  nand nand_438 (nand_438_out, nand_437_out, nand_427_out);
  and and_408 (and_408_out, nand_437_out, notconnected_3_out);
  nand nand_439 (nand_439_out, nand_430_out, nand_440_out);
  nand nand_440 (nand_440_out, nand_439_out, nand_431_out);
  and and_409 (and_409_out, nand_439_out, notconnected_3_out);
  // NotConnected on notconnected_10_out
  // NotConnected on notconnected_11_out
  // NotConnected on notconnected_12_out
  // NotConnected on notconnected_13_out
  and and_410 (and_410_out, notconnected_11_out[0], notconnected_11_out[0]);
  or or_92 (or_92_out, notconnected_12_out[0], notconnected_12_out[0]);
  xor xor_57 (xor_57_out, notconnected_13_out[0], notconnected_13_out[0]);
  and and_411 (and_411_out, notconnected_11_out[1], notconnected_11_out[1]);
  or or_93 (or_93_out, notconnected_12_out[1], notconnected_12_out[1]);
  xor xor_58 (xor_58_out, notconnected_13_out[1], notconnected_13_out[1]);
  not not_53 (not_53_out, notconnected_14_out);
  // NotConnected on notconnected_14_out
  and and_412 (and_412_out, notconnected_11_out[2], notconnected_11_out[2]);
  and and_413 (and_413_out, notconnected_11_out[3], notconnected_11_out[3]);
  or or_94 (or_94_out, notconnected_12_out[2], notconnected_12_out[2]);
  or or_95 (or_95_out, notconnected_12_out[3], notconnected_12_out[3]);
  xor xor_59 (xor_59_out, notconnected_13_out[2], notconnected_13_out[2]);
  xor xor_60 (xor_60_out, notconnected_13_out[3], notconnected_13_out[3]);
  // And and_414 has open pins: In_1=and_415_out, In_2=notconnected_10_out[7], out=open
  xor xor_61 (xor_61_out, notconnected_10_out[7], and_415_out);
  and and_415 (and_415_out, and_416_out, notconnected_10_out[6]);
  xor xor_62 (xor_62_out, notconnected_10_out[6], and_416_out);
  and and_416 (and_416_out, and_417_out, notconnected_10_out[5]);
  xor xor_63 (xor_63_out, notconnected_10_out[5], and_417_out);
  and and_417 (and_417_out, and_418_out, notconnected_10_out[4]);
  xor xor_64 (xor_64_out, notconnected_10_out[4], and_418_out);
  and and_418 (and_418_out, and_419_out, notconnected_10_out[3]);
  xor xor_65 (xor_65_out, notconnected_10_out[3], and_419_out);
  and and_419 (and_419_out, and_420_out, notconnected_10_out[2]);
  xor xor_66 (xor_66_out, notconnected_10_out[2], and_420_out);
  and and_420 (and_420_out, and_421_out, notconnected_10_out[1]);
  xor xor_67 (xor_67_out, notconnected_10_out[1], and_421_out);
  and and_421 (and_421_out, not_53_out, notconnected_10_out[0]);
  xor xor_68 (xor_68_out, notconnected_10_out[0], not_53_out);
  and and_422 (and_422_out, notconnected_11_out[4], notconnected_11_out[4]);
  or or_96 (or_96_out, notconnected_12_out[4], notconnected_12_out[4]);
  xor xor_69 (xor_69_out, notconnected_13_out[4], notconnected_13_out[4]);
  and and_423 (and_423_out, notconnected_11_out[5], notconnected_11_out[5]);
  or or_97 (or_97_out, notconnected_12_out[5], notconnected_12_out[5]);
  xor xor_70 (xor_70_out, notconnected_13_out[5], notconnected_13_out[5]);
  and and_424 (and_424_out, notconnected_11_out[6], notconnected_11_out[6]);
  and and_425 (and_425_out, notconnected_11_out[7], notconnected_11_out[7]);
  or or_98 (or_98_out, notconnected_12_out[6], notconnected_12_out[6]);
  or or_99 (or_99_out, notconnected_12_out[7], notconnected_12_out[7]);
  xor xor_71 (xor_71_out, notconnected_13_out[6], notconnected_13_out[6]);
  xor xor_72 (xor_72_out, notconnected_13_out[7], notconnected_13_out[7]);
  // NotConnected on notconnected_15_out
  // NotConnected on notconnected_16_out
  // NotConnected on notconnected_17_out
  // NotConnected on notconnected_18_out
  // NotConnected on notconnected_19_out
  // NotConnected on notconnected_20_out
  and and_426 (and_426_out, notconnected_21_out, notconnected_15_out[0]);
  nand nand_441 (nand_441_out, notconnected_16_out[0], notconnected_16_out[0]);
  nor nor_27 (nor_27_out, notconnected_17_out[0], notconnected_17_out[0]);
  not not_54 (not_54_out, notconnected_20_out);
  and and_427 (and_427_out, notconnected_21_out, notconnected_15_out[1]);
  and and_428 (and_428_out, notconnected_21_out, notconnected_15_out[2]);
  nand nand_442 (nand_442_out, notconnected_16_out[1], notconnected_16_out[1]);
  nand nand_443 (nand_443_out, notconnected_16_out[2], notconnected_16_out[2]);
  nor nor_28 (nor_28_out, notconnected_17_out[1], notconnected_17_out[1]);
  nor nor_29 (nor_29_out, notconnected_17_out[2], notconnected_17_out[2]);
  not not_55 (not_55_out, notconnected_19_out);
  not not_56 (not_56_out, notconnected_18_out);
  not not_57 (not_57_out, notconnected_20_out);
  not not_58 (not_58_out, notconnected_19_out);
  not not_59 (not_59_out, notconnected_18_out);
  not not_60 (not_60_out, not_54_out);
  // NotConnected on notconnected_21_out
  and and_429 (and_429_out, notconnected_21_out, notconnected_15_out[3]);
  nand nand_444 (nand_444_out, notconnected_16_out[3], notconnected_16_out[3]);
  nor nor_30 (nor_30_out, notconnected_17_out[3], notconnected_17_out[3]);
  and and_430 (and_430_out, not_56_out, not_55_out);
  and and_431 (and_431_out, notconnected_18_out, not_55_out);
  and and_432 (and_432_out, not_56_out, notconnected_19_out);
  and and_433 (and_433_out, notconnected_19_out, notconnected_18_out);
  and and_434 (and_434_out, not_59_out, not_58_out);
  and and_435 (and_435_out, notconnected_18_out, not_58_out);
  and and_436 (and_436_out, not_59_out, notconnected_19_out);
  and and_437 (and_437_out, notconnected_19_out, notconnected_18_out);
  and and_438 (and_438_out, notconnected_21_out, notconnected_15_out[4]);
  nand nand_445 (nand_445_out, notconnected_16_out[4], notconnected_16_out[4]);
  nor nor_31 (nor_31_out, notconnected_17_out[4], notconnected_17_out[4]);
  and and_439 (and_439_out, and_430_out, not_57_out);
  and and_440 (and_440_out, and_431_out, not_57_out);
  and and_441 (and_441_out, and_432_out, not_57_out);
  and and_442 (and_442_out, and_433_out, not_57_out);
  and and_443 (and_443_out, and_434_out, not_60_out);
  and and_444 (and_444_out, and_435_out, not_60_out);
  and and_445 (and_445_out, and_436_out, not_60_out);
  and and_446 (and_446_out, and_437_out, not_60_out);
  and and_447 (and_447_out, notconnected_21_out, notconnected_15_out[5]);
  and and_448 (and_448_out, notconnected_21_out, notconnected_15_out[6]);
  nand nand_446 (nand_446_out, notconnected_16_out[5], notconnected_16_out[5]);
  nand nand_447 (nand_447_out, notconnected_16_out[6], notconnected_16_out[6]);
  nor nor_32 (nor_32_out, notconnected_17_out[5], notconnected_17_out[5]);
  nor nor_33 (nor_33_out, notconnected_17_out[6], notconnected_17_out[6]);
  and and_449 (and_449_out, notconnected_21_out, notconnected_15_out[7]);
  nand nand_448 (nand_448_out, notconnected_16_out[7], notconnected_16_out[7]);
  nor nor_34 (nor_34_out, notconnected_17_out[7], notconnected_17_out[7]);

  // Notes on the sheet:
  //   DESTINATION sel
  //   Disable
  //   A_1
  //   A_0
  //   2x4 Demux
  //   Operation Decode
  //   Add
  //   Sub
  //   More
  //   Less
  //   MoreOrEqual
  //   LessOrEqual
  //   Always
  //   Never
  //   A3
  //   Immediate Arg 1
  //   Immediate Arg 2
  //   Arithmetic/Compare
  //   RAM
  //   Argument
  //   Arithmetic arguments
  //   A1
  //   A2
  //   3x8 Demux
  //   Arguments are listsed in order in decimal value
  //   Is0
  //   IsNot0
  //   Compare arguments
  //   ARG2 sel
  //   Many components are designed to
  //   take OPCODEs in and only use the
  //   last 3 argument bits.
  //   Arithmetic
  //   Compare
  //   Ram
  //   Main OPCODE Line
  //   ARG1 sel
  //   Immediates
  //   ARG2
  //   Immediate 2 Enable
  //   ARG1
  //   Immediate 1 Enable
  //   Immediate's Disable the corresponding argument
  //   Input
  //   SWITCH 2
  //   SWITCH 1
  //   Edge Register
  //   Clk
  //   Load A
  //   Load B
  //   D
  //   Load
  //   Edge Flop
  //   Latch
  //   Loaded
  //   Overwrite Value
  //   Overwrite
  //   COUNTER
  //   B
  //   Select
  //   MUX
  //   A
  //   INCRMNT
  //   SWITCH
  //   OR
  //   Conditional Unit
  //   Is less than 0 Unit
  //   Is!0 Unit
  //   ALU
  //   ADDER
  //   AND
  //   NAND
  //   NOR
  //   XOR
  //   .
  //   COMPONENTS
  //   Register - outdated
  //   Save
  //   Save Value
  //   1 Bit mem
  //   SaveVal
  //   Reset
  //   Write
  //   Always OUT
  //   OUT
  //   Always On Out
  //   Out
endmodule

/* Test case:
D C L ALWAYS LOADED
# 1. Randomized Startup: Register state is unknown (X). LOADED is 0 because L=0.
0x00 0 0 X 0x00

# 2. Load 0xAA: ALWAYS updates to 0xAA. LOADED shows it because L=1.
0xAA C 1 0xAA 0xAA

# 3. Transparent Check: ALWAYS stays 0xAA. LOADED drops to 0x00 because L=0.
0x55 0 0 0xAA 0x00
0x21 C 0 0x21 0x00

# 5. Load 0x00: Register becomes 0. Both pins show 0.
0x00 C 1 0x00 0x00

# 6. Edge-Triggering: Data 0xEE only moves to ALWAYS on the rising edge.
0xEE 0 1 0x00 0x00  # L=1, but no clock yet; LOADED is 0 because reg is 0
0xEE 1 1 0xEE 0xEE  # Clock goes high; Reg becomes 0xEE. LOADED now shows it.
0xDD 0 1 0xEE 0xEE  # Clock falls; Reg stays 0xEE.

# 7. High-Clock Stability Test
0xAA 0 1 0xEE 0xEE  # Prepare data 0xAA, but clock is 0. ALWAYS stays 0xEE.
0xAA 1 1 0xAA 0xAA  # Clock goes High. Register captures 0xAA.
0xFF 1 1 0xAA 0xAA  # DATA CHANGES TO 0xFF WHILE CLOCK IS STILL HIGH.
                    # ALWAYS MUST STAY 0xAA. If it changes to 0xFF, it's a latch!
*/

/* Test case:
In_3 In_2 In_1 Num_1 Out_0
0 0 0 4 0
0 0 1 5 1
0 0 0 210 0
0 0 1 253 1
0 1 1 65 0
0 1 0 102 1
0 1 1 237 1
0 1 0 179 0
1 0 0 102 1
1 0 0 0 1
1 0 0 252 0
1 0 1 179 1
1 0 1 0 1
1 0 1 112 0
1 1 0 0 1
1 1 0 243 1
1 1 0 123 1
1 1 1 0 0
1 1 1 243 0
1 1 1 123 0
*/

/* Test case:
C_2 C_1 C_0 A_0 B_0 O_0
0 0 1 9 6 15 #addition and subtraction
0 1 0 9 6 3
0 0 1 6 7 13
0 1 0 111 67 44
0 0 1 32 59 91
0 1 1 51 60 48  #and
0 1 1 3 2 2
0 1 1 5 3 1
0 1 1 12 25 8
0 1 1 4 8 0
1 0 1 5 3 7 #or
1 0 1 2 8 10
1 0 1 12 25 29
1 0 1 0 7 7
1 0 0 1 1 254 #nand
1 0 0 2 4 255
1 0 0 15 3 252
1 1 0 1 0 254 #nor
1 1 0 3 5 248
1 1 0 128 64 63
1 1 1 5 3 6 #xor
1 1 1 10 10 0
1 1 1 85 170 255
1 1 1 14 1 15
*/
