// Digital circuit overture.dig as structural Verilog
module overture (
  input  C_0,
  input  C_1,
  input  C_2,
  input  [7:0] A_0,
  input  [7:0] B_0,
  input  Clock,
  output [7:0] O_0
);

  wire and_7_out, and_8_out, and_9_out, and_10_out, and_11_out, and_12_out, and_13_out, and_14_out,
       and_16_out, and_17_out, and_18_out, and_19_out, and_21_out, and_22_out, and_23_out, and_24_out,
       and_67_out, and_68_out, and_69_out, and_70_out, and_71_out, and_72_out, and_73_out, and_74_out,
       and_79_out, and_80_out, and_81_out, and_82_out, and_83_out, and_84_out, and_85_out, and_89_out,
       and_90_out, and_91_out, and_92_out, and_93_out, and_94_out, and_95_out, and_96_out, and_97_out,
       and_98_out, and_99_out, and_100_out, and_101_out, and_102_out, and_103_out, and_104_out, and_105_out,
       and_106_out, and_107_out, and_108_out, and_109_out, and_110_out, and_111_out, and_112_out,
       and_113_out, and_114_out, and_115_out, and_116_out, and_117_out, and_118_out, and_119_out,
       and_120_out, and_122_out, and_123_out, and_124_out, and_125_out, and_126_out, and_127_out,
       and_128_out, and_129_out, and_130_out, and_131_out, and_132_out, and_133_out, and_134_out,
       and_135_out, and_136_out, and_137_out, and_138_out, and_139_out, and_140_out, and_141_out,
       and_142_out, and_143_out, and_144_out, and_145_out, and_146_out, and_147_out, and_148_out,
       and_149_out, and_150_out, and_151_out, and_152_out, and_153_out, and_154_out, and_155_out,
       and_156_out, and_157_out, and_158_out, and_159_out, and_160_out, and_161_out, and_162_out,
       and_163_out, and_164_out, and_165_out, and_166_out, and_167_out, and_168_out, and_169_out,
       and_170_out, and_171_out, and_172_out, and_173_out, and_174_out, and_175_out, and_177_out,
       and_178_out, and_179_out, and_180_out, and_181_out, and_182_out, and_183_out, and_184_out,
       and_185_out, and_186_out, and_187_out, and_188_out, and_189_out, and_190_out, and_191_out,
       and_192_out, and_193_out, and_194_out, and_195_out, and_196_out, and_197_out, and_198_out,
       and_199_out, and_200_out, and_201_out, and_202_out, and_203_out, and_204_out, and_205_out,
       and_206_out, and_207_out, and_208_out, and_209_out, and_210_out, and_211_out, dipswitch_1_out,
       dipswitch_2_out, dipswitch_3_out, nand_9_out, nand_10_out, nand_11_out, nand_12_out, nand_13_out,
       nand_14_out, nand_15_out, nand_16_out, nor_9_out, nor_10_out, nor_11_out, nor_12_out, nor_13_out,
       nor_14_out, nor_15_out, nor_16_out, nor_17_out, nor_18_out, nor_19_out, nor_20_out, nor_21_out,
       nor_22_out, nor_23_out, nor_24_out, nor_25_out, nor_26_out, nor_27_out, nor_28_out, nor_29_out,
       nor_30_out, nor_31_out, nor_32_out, nor_33_out, nor_34_out, nor_35_out, nor_36_out, nor_37_out,
       nor_38_out, nor_39_out, nor_40_out, nor_41_out, nor_42_out, nor_43_out, nor_44_out, nor_45_out,
       nor_46_out, nor_47_out, nor_48_out, nor_49_out, nor_50_out, not_1_out, not_2_out, not_3_out,
       not_4_out, not_5_out, not_6_out, not_7_out, not_8_out, not_9_out, not_10_out, not_11_out, not_12_out,
       not_13_out, not_14_out, not_15_out, not_16_out, not_17_out, not_18_out, not_19_out, not_20_out,
       not_21_out, not_22_out, not_23_out, not_24_out, not_25_out, not_26_out, not_27_out, not_28_out,
       not_29_out, not_30_out, not_31_out, not_32_out, not_33_out, notconnected_1_out, notconnected_5_out,
       notconnected_6_out, notconnected_7_out, notconnected_11_out, notconnected_16_out, notconnected_20_out,
       notconnected_21_out, notconnected_22_out, notconnected_23_out, or_8_out, or_9_out, or_10_out,
       or_11_out, or_12_out, or_13_out, or_14_out, or_15_out, or_17_out, or_58_out, or_59_out, or_60_out,
       or_61_out, or_62_out, or_63_out, or_64_out, or_65_out, or_66_out, or_67_out, or_68_out, or_69_out,
       or_70_out, or_71_out, or_72_out, or_73_out, undriven, xor_1_out, xor_2_out, xor_3_out, xor_4_out,
       xor_5_out, xor_6_out, xor_7_out, xor_8_out, xor_15_out, xor_16_out, xor_17_out, xor_18_out,
       xor_19_out, xor_20_out, xor_21_out, xor_22_out, xor_33_out, xor_34_out, xor_35_out, xor_36_out,
       xor_37_out, xor_38_out, xor_39_out, xor_40_out, xor_41_out, xor_42_out, xor_43_out, xor_44_out,
       xor_45_out, xor_46_out, xor_47_out, xor_48_out, xor_49_out, xor_50_out, xor_51_out, xor_52_out,
       xor_53_out, xor_54_out, xor_55_out, xor_56_out, xor_57_out, xor_58_out, xor_59_out, xor_60_out,
       xor_61_out, xor_62_out, xor_63_out, xor_64_out, xor_65_out, xor_66_out, xor_67_out, xor_68_out,
       xor_69_out, xor_70_out, xor_71_out, xor_72_out;
  wire [7:0] and_20_out, and_60_out, and_61_out, and_62_out, and_63_out, and_64_out, and_88_out, nand_8_out,
       nor_8_out, notconnected_2_out, notconnected_3_out, notconnected_4_out, notconnected_8_out,
       notconnected_9_out, notconnected_10_out, notconnected_12_out, notconnected_13_out,
       notconnected_14_out, notconnected_15_out, notconnected_17_out, notconnected_18_out,
       notconnected_19_out, or_16_out, or_54_out, or_55_out, or_56_out, or_57_out, xor_28_out, xor_32_out;

  xor xor_1 (xor_1_out, B_0[7], and_80_out);
  xor xor_2 (xor_2_out, B_0[6], and_80_out);
  xor xor_3 (xor_3_out, B_0[5], and_80_out);
  xor xor_4 (xor_4_out, B_0[4], and_80_out);
  xor xor_5 (xor_5_out, B_0[3], and_80_out);
  xor xor_6 (xor_6_out, B_0[2], and_80_out);
  xor xor_7 (xor_7_out, B_0[1], and_80_out);
  xor xor_8 (xor_8_out, B_0[0], and_80_out);
  and and_1 (and_20_out[0], B_0[0], A_0[0]);
  nand nand_1 (nand_8_out[0], B_0[0], A_0[0]);
  or or_1 (or_16_out[0], B_0[0], A_0[0]);
  nor nor_1 (nor_8_out[0], B_0[0], A_0[0]);
  xor xor_9 (xor_28_out[0], B_0[0], A_0[0]);
  and and_2 (and_20_out[1], B_0[1], A_0[1]);
  nand nand_2 (nand_8_out[1], B_0[1], A_0[1]);
  or or_2 (or_16_out[1], B_0[1], A_0[1]);
  nor nor_2 (nor_8_out[1], B_0[1], A_0[1]);
  xor xor_10 (xor_28_out[1], B_0[1], A_0[1]);
  and and_3 (and_20_out[2], B_0[2], A_0[2]);
  nand nand_3 (nand_8_out[2], B_0[2], A_0[2]);
  or or_3 (or_16_out[2], B_0[2], A_0[2]);
  nor nor_3 (nor_8_out[2], B_0[2], A_0[2]);
  xor xor_11 (xor_28_out[2], B_0[2], A_0[2]);
  and and_4 (and_20_out[3], B_0[3], A_0[3]);
  and and_5 (and_20_out[4], B_0[4], A_0[4]);
  nand nand_4 (nand_8_out[3], B_0[3], A_0[3]);
  nand nand_5 (nand_8_out[4], B_0[4], A_0[4]);
  or or_4 (or_16_out[3], B_0[3], A_0[3]);
  or or_5 (or_16_out[4], B_0[4], A_0[4]);
  nor nor_4 (nor_8_out[3], B_0[3], A_0[3]);
  nor nor_5 (nor_8_out[4], B_0[4], A_0[4]);
  xor xor_12 (xor_28_out[3], B_0[3], A_0[3]);
  xor xor_13 (xor_28_out[4], B_0[4], A_0[4]);
  and and_6 (and_20_out[5], B_0[5], A_0[5]);
  nand nand_6 (nand_8_out[5], B_0[5], A_0[5]);
  or or_6 (or_16_out[5], B_0[5], A_0[5]);
  nor nor_6 (nor_8_out[5], B_0[5], A_0[5]);
  xor xor_14 (xor_28_out[5], B_0[5], A_0[5]);
  and and_7 (and_7_out, xor_1_out, A_0[7]);
  xor xor_15 (xor_15_out, A_0[7], xor_1_out);
  and and_8 (and_8_out, xor_2_out, A_0[6]);
  xor xor_16 (xor_16_out, A_0[6], xor_2_out);
  and and_9 (and_9_out, xor_3_out, A_0[5]);
  xor xor_17 (xor_17_out, A_0[5], xor_3_out);
  and and_10 (and_10_out, xor_4_out, A_0[4]);
  xor xor_18 (xor_18_out, A_0[4], xor_4_out);
  and and_11 (and_11_out, xor_5_out, A_0[3]);
  xor xor_19 (xor_19_out, A_0[3], xor_5_out);
  and and_12 (and_12_out, xor_6_out, A_0[2]);
  xor xor_20 (xor_20_out, A_0[2], xor_6_out);
  and and_13 (and_13_out, xor_7_out, A_0[1]);
  xor xor_21 (xor_21_out, A_0[1], xor_7_out);
  and and_14 (and_14_out, xor_8_out, A_0[0]);
  xor xor_22 (xor_22_out, A_0[0], xor_8_out);
  and and_15 (and_20_out[6], B_0[6], A_0[6]);
  nand nand_7 (nand_8_out[6], B_0[6], A_0[6]);
  or or_7 (or_16_out[6], B_0[6], A_0[6]);
  nor nor_7 (nor_8_out[6], B_0[6], A_0[6]);
  xor xor_23 (xor_28_out[6], B_0[6], A_0[6]);
  or or_8 (or_8_out, and_7_out, and_16_out);
  and and_16 (and_16_out, xor_15_out, or_9_out);
  xor xor_24 (xor_32_out[7], xor_15_out, or_9_out);
  or or_9 (or_9_out, and_8_out, and_17_out);
  and and_17 (and_17_out, xor_16_out, or_10_out);
  xor xor_25 (xor_32_out[6], xor_16_out, or_10_out);
  or or_10 (or_10_out, and_9_out, and_18_out);
  and and_18 (and_18_out, xor_17_out, or_11_out);
  xor xor_26 (xor_32_out[5], xor_17_out, or_11_out);
  or or_11 (or_11_out, and_10_out, and_19_out);
  and and_19 (and_19_out, xor_18_out, or_12_out);
  xor xor_27 (xor_32_out[4], xor_18_out, or_12_out);
  or or_12 (or_12_out, and_11_out, and_21_out);
  or or_13 (or_13_out, and_12_out, and_22_out);
  or or_14 (or_14_out, and_13_out, and_23_out);
  or or_15 (or_15_out, and_14_out, and_24_out);
  and and_20 (and_20_out[7], B_0[7], A_0[7]);
  nand nand_8 (nand_8_out[7], B_0[7], A_0[7]);
  or or_16 (or_16_out[7], B_0[7], A_0[7]);
  nor nor_8 (nor_8_out[7], B_0[7], A_0[7]);
  xor xor_28 (xor_28_out[7], B_0[7], A_0[7]);
  and and_21 (and_21_out, xor_19_out, or_13_out);
  xor xor_29 (xor_32_out[3], xor_19_out, or_13_out);
  and and_22 (and_22_out, xor_20_out, or_14_out);
  xor xor_30 (xor_32_out[2], xor_20_out, or_14_out);
  and and_23 (and_23_out, xor_21_out, or_15_out);
  xor xor_31 (xor_32_out[1], xor_21_out, or_15_out);
  and and_24 (and_24_out, xor_22_out, and_80_out);
  xor xor_32 (xor_32_out[0], xor_22_out, and_80_out);
  and and_25 (and_60_out[0], and_81_out, and_20_out[0]);
  and and_26 (and_60_out[1], and_81_out, and_20_out[1]);
  and and_27 (and_61_out[0], and_82_out, nand_8_out[0]);
  and and_28 (and_61_out[1], and_82_out, nand_8_out[1]);
  and and_29 (and_62_out[0], and_83_out, or_16_out[0]);
  and and_30 (and_62_out[1], and_83_out, or_16_out[1]);
  and and_31 (and_63_out[0], and_84_out, nor_8_out[0]);
  and and_32 (and_63_out[1], and_84_out, nor_8_out[1]);
  and and_33 (and_64_out[0], and_85_out, xor_28_out[0]);
  and and_34 (and_64_out[1], and_85_out, xor_28_out[1]);
  and and_35 (and_60_out[2], and_81_out, and_20_out[2]);
  and and_36 (and_61_out[2], and_82_out, nand_8_out[2]);
  and and_37 (and_62_out[2], and_83_out, or_16_out[2]);
  and and_38 (and_63_out[2], and_84_out, nor_8_out[2]);
  and and_39 (and_64_out[2], and_85_out, xor_28_out[2]);
  and and_40 (and_60_out[3], and_81_out, and_20_out[3]);
  and and_41 (and_61_out[3], and_82_out, nand_8_out[3]);
  and and_42 (and_62_out[3], and_83_out, or_16_out[3]);
  and and_43 (and_63_out[3], and_84_out, nor_8_out[3]);
  and and_44 (and_64_out[3], and_85_out, xor_28_out[3]);
  and and_45 (and_60_out[4], and_81_out, and_20_out[4]);
  and and_46 (and_60_out[5], and_81_out, and_20_out[5]);
  and and_47 (and_61_out[4], and_82_out, nand_8_out[4]);
  and and_48 (and_61_out[5], and_82_out, nand_8_out[5]);
  and and_49 (and_62_out[4], and_83_out, or_16_out[4]);
  and and_50 (and_62_out[5], and_83_out, or_16_out[5]);
  and and_51 (and_63_out[4], and_84_out, nor_8_out[4]);
  and and_52 (and_63_out[5], and_84_out, nor_8_out[5]);
  and and_53 (and_64_out[4], and_85_out, xor_28_out[4]);
  and and_54 (and_64_out[5], and_85_out, xor_28_out[5]);
  and and_55 (and_60_out[6], and_81_out, and_20_out[6]);
  and and_56 (and_61_out[6], and_82_out, nand_8_out[6]);
  and and_57 (and_62_out[6], and_83_out, or_16_out[6]);
  and and_58 (and_63_out[6], and_84_out, nor_8_out[6]);
  and and_59 (and_64_out[6], and_85_out, xor_28_out[6]);
  and and_60 (and_60_out[7], and_81_out, and_20_out[7]);
  and and_61 (and_61_out[7], and_82_out, nand_8_out[7]);
  and and_62 (and_62_out[7], and_83_out, or_16_out[7]);
  and and_63 (and_63_out[7], and_84_out, nor_8_out[7]);
  and and_64 (and_64_out[7], and_85_out, xor_28_out[7]);
  not not_1 (not_1_out, C_2);
  and and_65 (and_88_out[0], or_17_out, xor_32_out[0]);
  not not_2 (not_2_out, C_1);
  not not_3 (not_3_out, C_1);
  and and_66 (and_88_out[1], or_17_out, xor_32_out[1]);
  not not_4 (not_4_out, C_0);
  and and_67 (and_67_out, not_4_out, not_2_out);
  and and_68 (and_68_out, C_0, not_2_out);
  and and_69 (and_69_out, not_4_out, C_1);
  and and_70 (and_70_out, C_1, C_0);
  not not_5 (not_5_out, C_2);
  not not_6 (not_6_out, C_0);
  and and_71 (and_71_out, not_6_out, not_3_out);
  and and_72 (and_72_out, C_0, not_3_out);
  and and_73 (and_73_out, not_6_out, C_1);
  and and_74 (and_74_out, C_1, C_0);
  not not_7 (not_7_out, not_1_out);
  and and_75 (and_88_out[2], or_17_out, xor_32_out[2]);
  and and_76 (and_88_out[3], or_17_out, xor_32_out[3]);
  and and_77 (and_88_out[4], or_17_out, xor_32_out[4]);
  // And and_78 has open pins: In_1=and_67_out, In_2=not_5_out, out=open
  and and_79 (and_79_out, and_68_out, not_5_out);
  and and_80 (and_80_out, and_69_out, not_5_out);
  and and_81 (and_81_out, and_70_out, not_5_out);
  and and_82 (and_82_out, and_71_out, not_7_out);
  and and_83 (and_83_out, and_72_out, not_7_out);
  and and_84 (and_84_out, and_73_out, not_7_out);
  and and_85 (and_85_out, and_74_out, not_7_out);
  and and_86 (and_88_out[5], or_17_out, xor_32_out[5]);
  and and_87 (and_88_out[6], or_17_out, xor_32_out[6]);
  and and_88 (and_88_out[7], or_17_out, xor_32_out[7]);
  or or_17 (or_17_out, and_79_out, and_80_out);
  or or_18 (O_0[0], and_88_out[0], or_54_out[0]);
  or or_19 (or_54_out[0], and_60_out[0], or_55_out[0]);
  or or_20 (or_55_out[0], and_61_out[0], or_56_out[0]);
  or or_21 (or_56_out[0], and_62_out[0], or_57_out[0]);
  or or_22 (or_57_out[0], and_63_out[0], and_64_out[0]);
  or or_23 (O_0[1], and_88_out[1], or_54_out[1]);
  or or_24 (or_54_out[1], and_60_out[1], or_55_out[1]);
  or or_25 (or_55_out[1], and_61_out[1], or_56_out[1]);
  or or_26 (or_56_out[1], and_62_out[1], or_57_out[1]);
  or or_27 (or_57_out[1], and_63_out[1], and_64_out[1]);
  or or_28 (O_0[2], and_88_out[2], or_54_out[2]);
  or or_29 (or_54_out[2], and_60_out[2], or_55_out[2]);
  or or_30 (or_55_out[2], and_61_out[2], or_56_out[2]);
  or or_31 (or_56_out[2], and_62_out[2], or_57_out[2]);
  or or_32 (or_57_out[2], and_63_out[2], and_64_out[2]);
  or or_33 (O_0[3], and_88_out[3], or_54_out[3]);
  or or_34 (O_0[4], and_88_out[4], or_54_out[4]);
  or or_35 (or_54_out[3], and_60_out[3], or_55_out[3]);
  or or_36 (or_54_out[4], and_60_out[4], or_55_out[4]);
  or or_37 (or_55_out[3], and_61_out[3], or_56_out[3]);
  or or_38 (or_55_out[4], and_61_out[4], or_56_out[4]);
  or or_39 (or_56_out[3], and_62_out[3], or_57_out[3]);
  or or_40 (or_56_out[4], and_62_out[4], or_57_out[4]);
  or or_41 (or_57_out[3], and_63_out[3], and_64_out[3]);
  or or_42 (or_57_out[4], and_63_out[4], and_64_out[4]);
  or or_43 (O_0[5], and_88_out[5], or_54_out[5]);
  or or_44 (or_54_out[5], and_60_out[5], or_55_out[5]);
  or or_45 (or_55_out[5], and_61_out[5], or_56_out[5]);
  or or_46 (or_56_out[5], and_62_out[5], or_57_out[5]);
  or or_47 (or_57_out[5], and_63_out[5], and_64_out[5]);
  or or_48 (O_0[6], and_88_out[6], or_54_out[6]);
  or or_49 (or_54_out[6], and_60_out[6], or_55_out[6]);
  or or_50 (or_55_out[6], and_61_out[6], or_56_out[6]);
  or or_51 (or_56_out[6], and_62_out[6], or_57_out[6]);
  or or_52 (or_57_out[6], and_63_out[6], and_64_out[6]);
  // NotConnected on notconnected_1_out
  // NotConnected on notconnected_2_out
  or or_53 (O_0[7], and_88_out[7], or_54_out[7]);
  or or_54 (or_54_out[7], and_60_out[7], or_55_out[7]);
  or or_55 (or_55_out[7], and_61_out[7], or_56_out[7]);
  or or_56 (or_56_out[7], and_62_out[7], or_57_out[7]);
  or or_57 (or_57_out[7], and_63_out[7], and_64_out[7]);
  // NotConnected on notconnected_3_out
  and and_89 (and_89_out, undriven, notconnected_3_out[0]);
  and and_90 (and_90_out, not_8_out, notconnected_1_out);
  not not_8 (not_8_out, notconnected_2_out[7]);
  and and_91 (and_91_out, notconnected_1_out, notconnected_2_out[7]);
  and and_92 (and_92_out, not_9_out, notconnected_1_out);
  not not_9 (not_9_out, notconnected_2_out[6]);
  and and_93 (and_93_out, notconnected_1_out, notconnected_2_out[6]);
  and and_94 (and_94_out, not_10_out, notconnected_1_out);
  not not_10 (not_10_out, notconnected_2_out[5]);
  and and_95 (and_95_out, notconnected_1_out, notconnected_2_out[5]);
  and and_96 (and_96_out, not_11_out, notconnected_1_out);
  not not_11 (not_11_out, notconnected_2_out[4]);
  and and_97 (and_97_out, notconnected_1_out, notconnected_2_out[4]);
  and and_98 (and_98_out, not_12_out, notconnected_1_out);
  not not_12 (not_12_out, notconnected_2_out[3]);
  and and_99 (and_99_out, notconnected_1_out, notconnected_2_out[3]);
  and and_100 (and_100_out, not_13_out, notconnected_1_out);
  not not_13 (not_13_out, notconnected_2_out[2]);
  and and_101 (and_101_out, notconnected_1_out, notconnected_2_out[2]);
  and and_102 (and_102_out, not_14_out, notconnected_1_out);
  not not_14 (not_14_out, notconnected_2_out[1]);
  and and_103 (and_103_out, notconnected_1_out, notconnected_2_out[1]);
  and and_104 (and_104_out, not_15_out, notconnected_1_out);
  not not_15 (not_15_out, notconnected_2_out[0]);
  and and_105 (and_105_out, notconnected_1_out, notconnected_2_out[0]);
  and and_106 (and_106_out, undriven, notconnected_3_out[1]);
  and and_107 (and_107_out, undriven, notconnected_3_out[2]);
  and and_108 (and_108_out, undriven, notconnected_3_out[3]);
  nor nor_9 (nor_9_out, and_90_out, nor_10_out);
  nor nor_10 (nor_10_out, nor_9_out, and_91_out);
  nor nor_11 (nor_11_out, and_92_out, nor_12_out);
  nor nor_12 (nor_12_out, nor_11_out, and_93_out);
  nor nor_13 (nor_13_out, and_94_out, nor_14_out);
  nor nor_14 (nor_14_out, nor_13_out, and_95_out);
  nor nor_15 (nor_15_out, and_96_out, nor_16_out);
  nor nor_16 (nor_16_out, nor_15_out, and_97_out);
  nor nor_17 (nor_17_out, and_98_out, nor_18_out);
  nor nor_18 (nor_18_out, nor_17_out, and_99_out);
  nor nor_19 (nor_19_out, and_100_out, nor_20_out);
  nor nor_20 (nor_20_out, nor_19_out, and_101_out);
  nor nor_21 (nor_21_out, and_102_out, nor_22_out);
  nor nor_22 (nor_22_out, nor_21_out, and_103_out);
  nor nor_23 (nor_23_out, and_104_out, nor_24_out);
  nor nor_24 (nor_24_out, nor_23_out, and_105_out);
  and and_109 (and_109_out, undriven, notconnected_3_out[4]);
  Reset reset_1 ();  // open: out
  and and_110 (and_110_out, nor_9_out, Clock);
  Reset reset_2 ();  // open: out
  and and_111 (and_111_out, nor_11_out, Clock);
  Reset reset_3 ();  // open: out
  and and_112 (and_112_out, nor_13_out, Clock);
  Reset reset_4 ();  // open: out
  and and_113 (and_113_out, nor_15_out, Clock);
  Reset reset_5 ();  // open: out
  and and_114 (and_114_out, nor_17_out, Clock);
  Reset reset_6 ();  // open: out
  and and_115 (and_115_out, nor_19_out, Clock);
  Reset reset_7 ();  // open: out
  and and_116 (and_116_out, nor_21_out, Clock);
  Reset reset_8 ();  // open: out
  and and_117 (and_117_out, nor_23_out, Clock);
  and and_118 (and_118_out, undriven, notconnected_3_out[5]);
  and and_119 (and_119_out, undriven, notconnected_3_out[6]);
  and and_120 (and_120_out, undriven, notconnected_3_out[7]);
  // NotConnected on notconnected_4_out
  not not_16 (not_16_out, notconnected_5_out);
  // NotConnected on notconnected_5_out
  // And and_121 has open pins: In_1=and_122_out, In_2=notconnected_4_out[7], out=open
  xor xor_33 (xor_33_out, notconnected_4_out[7], and_122_out);
  and and_122 (and_122_out, and_123_out, notconnected_4_out[6]);
  xor xor_34 (xor_34_out, notconnected_4_out[6], and_123_out);
  and and_123 (and_123_out, and_124_out, notconnected_4_out[5]);
  xor xor_35 (xor_35_out, notconnected_4_out[5], and_124_out);
  and and_124 (and_124_out, and_125_out, notconnected_4_out[4]);
  xor xor_36 (xor_36_out, notconnected_4_out[4], and_125_out);
  and and_125 (and_125_out, and_126_out, notconnected_4_out[3]);
  xor xor_37 (xor_37_out, notconnected_4_out[3], and_126_out);
  and and_126 (and_126_out, and_127_out, notconnected_4_out[2]);
  xor xor_38 (xor_38_out, notconnected_4_out[2], and_127_out);
  and and_127 (and_127_out, and_128_out, notconnected_4_out[1]);
  xor xor_39 (xor_39_out, notconnected_4_out[1], and_128_out);
  and and_128 (and_128_out, not_16_out, notconnected_4_out[0]);
  xor xor_40 (xor_40_out, notconnected_4_out[0], not_16_out);
  // NotConnected on notconnected_6_out
  // NotConnected on notconnected_7_out
  // NotConnected on notconnected_8_out
  // NotConnected on notconnected_9_out
  // NotConnected on notconnected_10_out
  DipSwitch dipswitch_1 (.out(dipswitch_1_out));
  DipSwitch dipswitch_2 (.out(dipswitch_2_out));
  DipSwitch dipswitch_3 (.out(dipswitch_3_out));
  not not_17 (not_17_out, notconnected_8_out[7]);
  and and_129 (and_129_out, notconnected_6_out, notconnected_8_out[7]);
  not not_18 (not_18_out, notconnected_8_out[6]);
  and and_130 (and_130_out, notconnected_6_out, notconnected_8_out[6]);
  not not_19 (not_19_out, notconnected_8_out[5]);
  and and_131 (and_131_out, notconnected_6_out, notconnected_8_out[5]);
  not not_20 (not_20_out, notconnected_8_out[4]);
  and and_132 (and_132_out, notconnected_6_out, notconnected_8_out[4]);
  not not_21 (not_21_out, notconnected_8_out[3]);
  and and_133 (and_133_out, notconnected_6_out, notconnected_8_out[3]);
  not not_22 (not_22_out, notconnected_8_out[2]);
  and and_134 (and_134_out, notconnected_6_out, notconnected_8_out[2]);
  not not_23 (not_23_out, notconnected_8_out[1]);
  and and_135 (and_135_out, notconnected_6_out, notconnected_8_out[1]);
  not not_24 (not_24_out, notconnected_8_out[0]);
  and and_136 (and_136_out, notconnected_6_out, notconnected_8_out[0]);
  and and_137 (and_137_out, not_25_out, dipswitch_2_out);
  not not_25 (not_25_out, dipswitch_3_out);
  and and_138 (and_138_out, dipswitch_2_out, dipswitch_3_out);
  and and_139 (and_139_out, not_17_out, notconnected_6_out);
  and and_140 (and_140_out, not_18_out, notconnected_6_out);
  and and_141 (and_141_out, not_19_out, notconnected_6_out);
  and and_142 (and_142_out, not_20_out, notconnected_6_out);
  and and_143 (and_143_out, not_21_out, notconnected_6_out);
  and and_144 (and_144_out, not_22_out, notconnected_6_out);
  and and_145 (and_145_out, not_23_out, notconnected_6_out);
  and and_146 (and_146_out, not_24_out, notconnected_6_out);
  nor nor_25 (nor_25_out, and_139_out, nor_26_out);
  nor nor_26 (nor_26_out, nor_25_out, and_129_out);
  nor nor_27 (nor_27_out, and_140_out, nor_28_out);
  nor nor_28 (nor_28_out, nor_27_out, and_130_out);
  nor nor_29 (nor_29_out, and_141_out, nor_30_out);
  nor nor_30 (nor_30_out, nor_29_out, and_131_out);
  nor nor_31 (nor_31_out, and_142_out, nor_32_out);
  nor nor_32 (nor_32_out, nor_31_out, and_132_out);
  nor nor_33 (nor_33_out, and_143_out, nor_34_out);
  nor nor_34 (nor_34_out, nor_33_out, and_133_out);
  nor nor_35 (nor_35_out, and_144_out, nor_36_out);
  nor nor_36 (nor_36_out, nor_35_out, and_134_out);
  nor nor_37 (nor_37_out, and_145_out, nor_38_out);
  nor nor_38 (nor_38_out, nor_37_out, and_135_out);
  nor nor_39 (nor_39_out, and_146_out, nor_40_out);
  nor nor_40 (nor_40_out, nor_39_out, and_136_out);
  and and_147 (and_147_out, notconnected_9_out[7], notconnected_10_out[7]);
  xor xor_41 (xor_41_out, notconnected_10_out[7], notconnected_9_out[7]);
  and and_148 (and_148_out, notconnected_9_out[6], notconnected_10_out[6]);
  xor xor_42 (xor_42_out, notconnected_10_out[6], notconnected_9_out[6]);
  and and_149 (and_149_out, notconnected_9_out[5], notconnected_10_out[5]);
  xor xor_43 (xor_43_out, notconnected_10_out[5], notconnected_9_out[5]);
  and and_150 (and_150_out, notconnected_9_out[4], notconnected_10_out[4]);
  xor xor_44 (xor_44_out, notconnected_10_out[4], notconnected_9_out[4]);
  and and_151 (and_151_out, notconnected_9_out[3], notconnected_10_out[3]);
  xor xor_45 (xor_45_out, notconnected_10_out[3], notconnected_9_out[3]);
  and and_152 (and_152_out, notconnected_9_out[2], notconnected_10_out[2]);
  xor xor_46 (xor_46_out, notconnected_10_out[2], notconnected_9_out[2]);
  and and_153 (and_153_out, notconnected_9_out[1], notconnected_10_out[1]);
  xor xor_47 (xor_47_out, notconnected_10_out[1], notconnected_9_out[1]);
  and and_154 (and_154_out, notconnected_9_out[0], notconnected_10_out[0]);
  xor xor_48 (xor_48_out, notconnected_10_out[0], notconnected_9_out[0]);
  nor nor_41 (nor_41_out, and_137_out, nor_42_out);
  nor nor_42 (nor_42_out, nor_41_out, and_138_out);
  or or_58 (or_58_out, and_147_out, and_155_out);
  and and_155 (and_155_out, xor_41_out, or_59_out);
  xor xor_49 (xor_49_out, xor_41_out, or_59_out);
  or or_59 (or_59_out, and_148_out, and_156_out);
  and and_156 (and_156_out, xor_42_out, or_60_out);
  xor xor_50 (xor_50_out, xor_42_out, or_60_out);
  or or_60 (or_60_out, and_149_out, and_157_out);
  and and_157 (and_157_out, xor_43_out, or_61_out);
  xor xor_51 (xor_51_out, xor_43_out, or_61_out);
  or or_61 (or_61_out, and_150_out, and_158_out);
  and and_158 (and_158_out, xor_44_out, or_62_out);
  xor xor_52 (xor_52_out, xor_44_out, or_62_out);
  or or_62 (or_62_out, and_151_out, and_167_out);
  or or_63 (or_63_out, and_152_out, and_168_out);
  or or_64 (or_64_out, and_153_out, and_169_out);
  or or_65 (or_65_out, and_154_out, and_170_out);
  // NotConnected on notconnected_11_out
  Reset reset_9 ();  // open: out
  Reset reset_10 ();  // open: out
  and and_159 (and_159_out, nor_25_out, notconnected_7_out);
  Reset reset_11 ();  // open: out
  and and_160 (and_160_out, nor_27_out, notconnected_7_out);
  Reset reset_12 ();  // open: out
  and and_161 (and_161_out, nor_29_out, notconnected_7_out);
  Reset reset_13 ();  // open: out
  and and_162 (and_162_out, nor_31_out, notconnected_7_out);
  Reset reset_14 ();  // open: out
  and and_163 (and_163_out, nor_33_out, notconnected_7_out);
  Reset reset_15 ();  // open: out
  and and_164 (and_164_out, nor_35_out, notconnected_7_out);
  Reset reset_16 ();  // open: out
  and and_165 (and_165_out, nor_37_out, notconnected_7_out);
  Reset reset_17 ();  // open: out
  and and_166 (and_166_out, nor_39_out, notconnected_7_out);
  and and_167 (and_167_out, xor_45_out, or_63_out);
  xor xor_53 (xor_53_out, xor_45_out, or_63_out);
  and and_168 (and_168_out, xor_46_out, or_64_out);
  xor xor_54 (xor_54_out, xor_46_out, or_64_out);
  and and_169 (and_169_out, xor_47_out, or_65_out);
  xor xor_55 (xor_55_out, xor_47_out, or_65_out);
  and and_170 (and_170_out, xor_48_out, notconnected_11_out);
  xor xor_56 (xor_56_out, xor_48_out, notconnected_11_out);
  and and_171 (and_171_out, nor_41_out, dipswitch_1_out);
  // NotConnected on notconnected_12_out
  // NotConnected on notconnected_13_out
  // NotConnected on notconnected_14_out
  // NotConnected on notconnected_15_out
  and and_172 (and_172_out, notconnected_13_out[0], notconnected_13_out[0]);
  or or_66 (or_66_out, notconnected_14_out[0], notconnected_14_out[0]);
  xor xor_57 (xor_57_out, notconnected_15_out[0], notconnected_15_out[0]);
  and and_173 (and_173_out, notconnected_13_out[1], notconnected_13_out[1]);
  or or_67 (or_67_out, notconnected_14_out[1], notconnected_14_out[1]);
  xor xor_58 (xor_58_out, notconnected_15_out[1], notconnected_15_out[1]);
  not not_26 (not_26_out, notconnected_16_out);
  // NotConnected on notconnected_16_out
  and and_174 (and_174_out, notconnected_13_out[2], notconnected_13_out[2]);
  and and_175 (and_175_out, notconnected_13_out[3], notconnected_13_out[3]);
  or or_68 (or_68_out, notconnected_14_out[2], notconnected_14_out[2]);
  or or_69 (or_69_out, notconnected_14_out[3], notconnected_14_out[3]);
  xor xor_59 (xor_59_out, notconnected_15_out[2], notconnected_15_out[2]);
  xor xor_60 (xor_60_out, notconnected_15_out[3], notconnected_15_out[3]);
  // And and_176 has open pins: In_1=and_177_out, In_2=notconnected_12_out[7], out=open
  xor xor_61 (xor_61_out, notconnected_12_out[7], and_177_out);
  and and_177 (and_177_out, and_178_out, notconnected_12_out[6]);
  xor xor_62 (xor_62_out, notconnected_12_out[6], and_178_out);
  and and_178 (and_178_out, and_179_out, notconnected_12_out[5]);
  xor xor_63 (xor_63_out, notconnected_12_out[5], and_179_out);
  and and_179 (and_179_out, and_180_out, notconnected_12_out[4]);
  xor xor_64 (xor_64_out, notconnected_12_out[4], and_180_out);
  and and_180 (and_180_out, and_181_out, notconnected_12_out[3]);
  xor xor_65 (xor_65_out, notconnected_12_out[3], and_181_out);
  and and_181 (and_181_out, and_182_out, notconnected_12_out[2]);
  xor xor_66 (xor_66_out, notconnected_12_out[2], and_182_out);
  and and_182 (and_182_out, and_183_out, notconnected_12_out[1]);
  xor xor_67 (xor_67_out, notconnected_12_out[1], and_183_out);
  and and_183 (and_183_out, not_26_out, notconnected_12_out[0]);
  xor xor_68 (xor_68_out, notconnected_12_out[0], not_26_out);
  and and_184 (and_184_out, notconnected_13_out[4], notconnected_13_out[4]);
  or or_70 (or_70_out, notconnected_14_out[4], notconnected_14_out[4]);
  xor xor_69 (xor_69_out, notconnected_15_out[4], notconnected_15_out[4]);
  and and_185 (and_185_out, notconnected_13_out[5], notconnected_13_out[5]);
  or or_71 (or_71_out, notconnected_14_out[5], notconnected_14_out[5]);
  xor xor_70 (xor_70_out, notconnected_15_out[5], notconnected_15_out[5]);
  and and_186 (and_186_out, notconnected_13_out[6], notconnected_13_out[6]);
  and and_187 (and_187_out, notconnected_13_out[7], notconnected_13_out[7]);
  or or_72 (or_72_out, notconnected_14_out[6], notconnected_14_out[6]);
  or or_73 (or_73_out, notconnected_14_out[7], notconnected_14_out[7]);
  xor xor_71 (xor_71_out, notconnected_15_out[6], notconnected_15_out[6]);
  xor xor_72 (xor_72_out, notconnected_15_out[7], notconnected_15_out[7]);
  // NotConnected on notconnected_17_out
  // NotConnected on notconnected_18_out
  // NotConnected on notconnected_19_out
  // NotConnected on notconnected_20_out
  // NotConnected on notconnected_21_out
  // NotConnected on notconnected_22_out
  and and_188 (and_188_out, notconnected_23_out, notconnected_17_out[0]);
  nand nand_9 (nand_9_out, notconnected_18_out[0], notconnected_18_out[0]);
  nor nor_43 (nor_43_out, notconnected_19_out[0], notconnected_19_out[0]);
  not not_27 (not_27_out, notconnected_22_out);
  and and_189 (and_189_out, notconnected_23_out, notconnected_17_out[1]);
  and and_190 (and_190_out, notconnected_23_out, notconnected_17_out[2]);
  nand nand_10 (nand_10_out, notconnected_18_out[1], notconnected_18_out[1]);
  nand nand_11 (nand_11_out, notconnected_18_out[2], notconnected_18_out[2]);
  nor nor_44 (nor_44_out, notconnected_19_out[1], notconnected_19_out[1]);
  nor nor_45 (nor_45_out, notconnected_19_out[2], notconnected_19_out[2]);
  not not_28 (not_28_out, notconnected_21_out);
  not not_29 (not_29_out, notconnected_20_out);
  not not_30 (not_30_out, notconnected_22_out);
  not not_31 (not_31_out, notconnected_21_out);
  not not_32 (not_32_out, notconnected_20_out);
  not not_33 (not_33_out, not_27_out);
  // NotConnected on notconnected_23_out
  and and_191 (and_191_out, notconnected_23_out, notconnected_17_out[3]);
  nand nand_12 (nand_12_out, notconnected_18_out[3], notconnected_18_out[3]);
  nor nor_46 (nor_46_out, notconnected_19_out[3], notconnected_19_out[3]);
  and and_192 (and_192_out, not_29_out, not_28_out);
  and and_193 (and_193_out, notconnected_20_out, not_28_out);
  and and_194 (and_194_out, not_29_out, notconnected_21_out);
  and and_195 (and_195_out, notconnected_21_out, notconnected_20_out);
  and and_196 (and_196_out, not_32_out, not_31_out);
  and and_197 (and_197_out, notconnected_20_out, not_31_out);
  and and_198 (and_198_out, not_32_out, notconnected_21_out);
  and and_199 (and_199_out, notconnected_21_out, notconnected_20_out);
  and and_200 (and_200_out, notconnected_23_out, notconnected_17_out[4]);
  nand nand_13 (nand_13_out, notconnected_18_out[4], notconnected_18_out[4]);
  nor nor_47 (nor_47_out, notconnected_19_out[4], notconnected_19_out[4]);
  and and_201 (and_201_out, and_192_out, not_30_out);
  and and_202 (and_202_out, and_193_out, not_30_out);
  and and_203 (and_203_out, and_194_out, not_30_out);
  and and_204 (and_204_out, and_195_out, not_30_out);
  and and_205 (and_205_out, and_196_out, not_33_out);
  and and_206 (and_206_out, and_197_out, not_33_out);
  and and_207 (and_207_out, and_198_out, not_33_out);
  and and_208 (and_208_out, and_199_out, not_33_out);
  and and_209 (and_209_out, notconnected_23_out, notconnected_17_out[5]);
  and and_210 (and_210_out, notconnected_23_out, notconnected_17_out[6]);
  nand nand_14 (nand_14_out, notconnected_18_out[5], notconnected_18_out[5]);
  nand nand_15 (nand_15_out, notconnected_18_out[6], notconnected_18_out[6]);
  nor nor_48 (nor_48_out, notconnected_19_out[5], notconnected_19_out[5]);
  nor nor_49 (nor_49_out, notconnected_19_out[6], notconnected_19_out[6]);
  and and_211 (and_211_out, notconnected_23_out, notconnected_17_out[7]);
  nand nand_16 (nand_16_out, notconnected_18_out[7], notconnected_18_out[7]);
  nor nor_50 (nor_50_out, notconnected_19_out[7], notconnected_19_out[7]);

  // Notes on the sheet:
  //   B
  //   A
  //   ALU
  //   ADDER
  //   AND
  //   NAND
  //   OR
  //   NOR
  //   XOR
  //   .
  //   SWITCH
  //   3x8 Demux
  //   A1
  //   A2
  //   A3
  //   2x4 Demux
  //   A_0
  //   A_1
  //   Disable
  //   Register
  //   Save
  //   Load
  //   Save Value
  //   1 Bit mem
  //   Always On Out
  //   Out
  //   INCRMNT
  //   SaveVal
  //   Reset
  //   Write
  //   Always OUT
  //   OUT
endmodule

/* Test case:
C_2 C_1 C_0 A_0 B_0 O_0
0 0 1 9 6 15 #addition and subtraction
0 1 0 9 6 3
0 0 1 6 7 13
0 1 0 111 67 44
0 0 1 32 59 91
0 1 1 51 60 48  #and
0 1 1 3 2 2
0 1 1 5 3 1
0 1 1 12 25 8
0 1 1 4 8 0
1 0 1 5 3 7 #or
1 0 1 2 8 10
1 0 1 12 25 29
1 0 1 0 7 7
1 0 0 1 1 254 #nand
1 0 0 2 4 255
1 0 0 15 3 252
1 1 0 1 0 254 #nor
1 1 0 3 5 248
1 1 0 128 64 63
1 1 1 5 3 6 #xor
1 1 1 10 10 0
1 1 1 85 170 255
1 1 1 14 1 15
*/
